// Digital circuit PDP8-X.dig as structural Verilog
module PDP8_X (
  input  clk
);

  wire AC2RAMD, AC_CK, add_1_c_o, add_2_c_o, AND, and_1_out, and_3_out, and_4_out, and_7_out, and_8_out,
       and_9_out, and_10_out, and_11_out, and_12_out, and_14_out, and_17_out, and_18_out, and_19_out,
       and_20_out, and_21_out, and_22_out, and_23_out, and_24_out, and_26_out, and_27_out, and_28_out,
       and_29_out, and_30_out, and_32_out, and_33_out, and_34_out, and_35_out, and_36_out, and_37_out,
       and_38_out, and_39_out, and_40_out, and_41_out, and_42_out, and_43_out, and_44_out, and_45_out,
       and_46_out, and_47_out, and_48_out, and_49_out, and_51_out, and_52_out, and_53_out, and_54_out,
       and_55_out, and_57_out, and_58_out, and_59_out, and_60_out, and_61_out, and_62_out, and_63_out,
       and_64_out, and_65_out, and_66_out, and_69_out, and_70_out, and_73_out, and_74_out, and_75_out,
       and_76_out, and_78_out, and_79_out, and_80_out, and_81_out, and_82_out, and_83_out, and_84_out,
       and_85_out, and_86_out, and_87_out, and_88_out, and_89_out, and_91_out, and_92_out, and_93_out,
       and_94_out, and_96_out, and_97_out, and_99_out, and_100_out, and_101_out, and_102_out, and_104_out,
       and_105_out, and_106_out, and_107_out, and_108_out, and_109_out, and_110_out, and_111_out,
       and_113_out, and_114_out, and_115_out, and_116_out, and_117_out, and_118_out, and_119_out,
       and_120_out, and_121_out, and_123_out, and_125_out, and_126_out, and_127_out, and_128_out,
       and_129_out, and_130_out, and_131_out, and_132_out, and_133_out, and_134_out, and_136_out,
       and_138_out, and_140_out, and_141_out, and_142_out, and_143_out, and_144_out, and_146_out,
       and_148_out, and_149_out, and_150_out, and_152_out, and_153_out, and_154_out, and_155_out,
       and_156_out, and_157_out, and_178_out, and_182_out, and_184_out, AUTOIND, BP_ENABLED_b, CK0, CK1, CK2,
       CK3, CK4, CK5, CK6, CK7, CK8, CK9, CLA, CLA_KCC, CLAx, CLL, CNT_AND, CNT_AND_I, CNT_AND_IA, CNT_DCA,
       CNT_DCA_I, CNT_DCA_IA, CNT_ISZ, CNT_ISZ_I, CNT_ISZ_IA, CNT_JMP, CNT_JMP_I, CNT_JMP_IA, CNT_JMS,
       CNT_JMS_I, CNT_JMS_IA, CNT_OPR1, CNT_OPR2, CNT_OPR3, CNT_TAD, CNT_TAD_I, CNT_TAD_IA, comparator_1_eq,
       comparator_2_eq, counter_1_o1, counter_1_o2, counter_1_o3, counter_1_o4, counter_1_o5, counter_1_o6,
       counter_1_o7, counter_1_o8, counter_1_o9, counter_1_o10, counter_1_o11, counter_1_o12, counter_1_o13,
       counter_1_o14, counter_1_o15, counter_1_o16, counter_1_o17, counter_1_o18, counter_1_o19,
       counter_1_o20, counter_1_o21, counter_1_o22, counter_1_o23, counter_1_o24, counter_1_o25,
       counter_1_o26, counter_1_o27, counter_1_o28, counter_1_o29, counter_1_o30, counter_1_o31,
       counter_1_o32, counter_2_ovf, d_ff_1_q, d_ff_as_2_q, DATA_CK, DCA, demultiplexer_1_out_3,
       demultiplexer_1_out_7, demultiplexer_2_out_3, demultiplexer_2_out_7, demultiplexer_4_out_10,
       demultiplexer_4_out_11, demultiplexer_4_out_12, demultiplexer_4_out_13, demultiplexer_4_out_14,
       demultiplexer_4_out_15, demultiplexer_4_out_16, demultiplexer_4_out_17, demultiplexer_4_out_18,
       demultiplexer_4_out_19, demultiplexer_4_out_20, demultiplexer_4_out_21, demultiplexer_4_out_22,
       demultiplexer_4_out_23, demultiplexer_4_out_24, demultiplexer_4_out_25, demultiplexer_4_out_26,
       demultiplexer_4_out_27, demultiplexer_4_out_28, demultiplexer_4_out_29, demultiplexer_4_out_30,
       demultiplexer_4_out_31, demultiplexer_4_out_32, demultiplexer_4_out_33, demultiplexer_4_out_34,
       demultiplexer_4_out_35, demultiplexer_4_out_36, demultiplexer_4_out_37, demultiplexer_4_out_38,
       demultiplexer_4_out_39, demultiplexer_4_out_40, demultiplexer_4_out_41, demultiplexer_4_out_42,
       demultiplexer_4_out_43, demultiplexer_4_out_44, demultiplexer_4_out_45, demultiplexer_4_out_46,
       demultiplexer_4_out_47, demultiplexer_4_out_48, demultiplexer_4_out_49, demultiplexer_4_out_50,
       demultiplexer_4_out_51, demultiplexer_4_out_52, demultiplexer_4_out_53, demultiplexer_4_out_54,
       demultiplexer_4_out_55, demultiplexer_4_out_56, demultiplexer_4_out_57, demultiplexer_4_out_58,
       demultiplexer_4_out_59, demultiplexer_4_out_60, demultiplexer_4_out_61, demultiplexer_4_out_62,
       demultiplexer_4_out_63, demultiplexer_6_out_0, demultiplexer_6_out_1, demultiplexer_7_out_3,
       demultiplexer_7_out_7, demultiplexer_8_out_3, demultiplexer_8_out_7, demultiplexer_10_out_10,
       demultiplexer_10_out_11, demultiplexer_10_out_12, demultiplexer_10_out_13, demultiplexer_10_out_14,
       demultiplexer_10_out_15, demultiplexer_10_out_16, demultiplexer_10_out_17, demultiplexer_10_out_18,
       demultiplexer_10_out_19, demultiplexer_10_out_20, demultiplexer_10_out_21, demultiplexer_10_out_22,
       demultiplexer_10_out_23, demultiplexer_10_out_24, demultiplexer_10_out_25, demultiplexer_10_out_26,
       demultiplexer_10_out_27, demultiplexer_10_out_28, demultiplexer_10_out_29, demultiplexer_10_out_30,
       demultiplexer_10_out_31, demultiplexer_10_out_32, demultiplexer_10_out_33, demultiplexer_10_out_34,
       demultiplexer_10_out_35, demultiplexer_10_out_36, demultiplexer_10_out_37, demultiplexer_10_out_38,
       demultiplexer_10_out_39, demultiplexer_10_out_40, demultiplexer_10_out_41, demultiplexer_10_out_42,
       demultiplexer_10_out_43, demultiplexer_10_out_44, demultiplexer_10_out_45, demultiplexer_10_out_46,
       demultiplexer_10_out_47, demultiplexer_10_out_48, demultiplexer_10_out_49, demultiplexer_10_out_50,
       demultiplexer_10_out_51, demultiplexer_10_out_52, demultiplexer_10_out_53, demultiplexer_10_out_54,
       demultiplexer_10_out_55, demultiplexer_10_out_56, demultiplexer_10_out_57, demultiplexer_10_out_58,
       demultiplexer_10_out_59, demultiplexer_10_out_60, demultiplexer_10_out_61, demultiplexer_10_out_62,
       demultiplexer_10_out_63, driver_2_out, driver_224_out, driver_227_out, driver_228_out, driver_229_out,
       driver_233_out, driver_234_out, driver_238_out, driver_239_out, FLAG_GIE, FLAG_KBD, FLAG_KBDIE,
       FLAG_PRN, FORCE4000, H_out, HALT, HLT_ENABLED_b, i_cla, i_cll, i_cma, i_cml, i_hlt, i_iac, i_nop,
       i_osr, I_out, i_ral, i_rar, i_rtl, i_rtr, i_skp, i_sma, i_sna, i_snl, i_spa, i_sza, i_szl, INC2RAMD,
       INCZERO, IND, IND2INC, IND2PC, IND2RAMA, IND_CK, IOT, IOT_CAF, IOT_DEV1x, IOT_DEV2x, IOT_DEV3x,
       IOT_DEV4x, IOT_DEV5, IOT_DEV5x, IOT_DEV6, IOT_DEV6x, IOT_DEV7, IOT_DEV8, IOT_DEV9, IOT_DEVCPU,
       IOT_DEVHSP, IOT_DEVHSR, IOT_DEVKBD, IOT_DEVPRI, IOT_GTF, IOT_IOF, IOT_ION, IOT_KCC, IOT_KCF, IOT_KIE,
       IOT_KRB, IOT_KRS, IOT_KSF, IOT_RTF, IOT_SGT, IOT_SKON, IOT_SRQ, IOT_TCF, IOT_TFL, IOT_TLS, IOT_TPC,
       IOT_TSF, IOT_TSK, IR2PC, IR2RAMA, IR_CK, IRQ_BUS, IRQ_INHIBIT, IRQ_JMS, ISZ, JMP, JMS, KEYBOARD_av,
       L_CAF, L_DEV1x, L_DEV2x, L_DEV3x, L_DEV4x, L_DEV5, L_DEV5x, L_DEV6, L_DEV6x, L_DEV7, L_DEV8, L_DEV9,
       L_DEVCPU, L_DEVHSP, L_DEVHSR, L_DEVKBD, L_DEVPRI, L_GTF, L_IOF, L_ION, L_KCC, L_KCF, L_KIE, L_KRB,
       L_KRS, L_KSF, L_RTF, L_SGT, L_SKON, L_SRQ, L_TCF, L_TFL, L_TLS, L_TPC, L_TSF, L_TSK, LD2INC, LINK,
       LINK_CK, monoflop_1_q, monoflop_2_q, monoflop_3_nq, monoflop_4_q, MP, MQ_CK, nand_1_out, NOIND,
       nor_1_out, nor_2_out, nor_3_out, nor_4_out, not_1_out, not_2_out, not_4_out, not_5_out, not_6_out,
       OPR, OPR1, OPR2, OPR3, OPR_ASL, OPR_CLA1, OPR_CLA2, OPR_CLA3, OPR_CLL, OPR_CMA, OPR_CML, OPR_DVI,
       OPR_HLT, OPR_IAC, OPR_LEFT, OPR_LSR, OPR_MQA, OPR_MQL, OPR_MUY, OPR_NA1, OPR_NMI, OPR_NOP,
       OPR_OPERATION, OPR_OSR, OPR_RIGHT, OPR_SCA, OPR_SCL, OPR_SHL, OPR_SMASPA, OPR_SNLSZL, OPR_SWP,
       OPR_SZASNA, OPR_TSTINV, OPR_X2, or_1_out, or_2_out, or_3_out, or_4_out, or_6_out, or_7_out, or_8_out,
       or_9_out, or_10_out, or_11_out, or_12_out, or_14_out, or_15_out, or_16_out, or_17_out, or_18_out,
       or_19_out, OR_KBD12, OR_STATUS12, PC2ADDR, PC2RAMD, PC_CK, PC_eq_200, PC_LD, PH_FIRST, PH_LAST,
       PH_STB, R_out, RAM_OE, RAM_WE, RAMA_HOLD, RAMD2AC_ADD, RAMD2AC_AND, RAMD2IND, RAMD2PC, reset_1_out,
       ROT2AC, rotater_1_p5, rs_ff_as_1_q, rs_ff_as_2_q, RTF_IOF, RTF_ION, RTF_LINK, S_out, SKIP, STB0, STB1,
       STB2, STB3, STB4, STB5, STB6, STB7, STB8, STB9, TAD, TAD_OVF_q, xor_1_out, xor_2_out, xor_3_out,
       xor_4_out, xor_6_out;
  wire [2:0] and_179_out, DA0, DA1, DA2, DA3, IND0, IND1, IND2, IND3, RA0, RA1, RA2, RA3;
  wire [3:0] CK_NUM;
  wire [4:0] counter_2_out;
  wire [11:0] AC, add_1_s, add_2_s, and_2_out, and_5_out, and_6_out, autocapture_1__10, autocapture_1__11,
       autocapture_1__12, autocapture_1__13, autocapture_1__14, autocapture_1__15, autocapture_1__16,
       autocapture_1__17, bitextender_1_out, bitextender_2_out, bitextender_3_out, BUS_IR, BUS_PC,
       dipswitch_1_out, driver_6_out, driver_15_out, driver_21_out, INC_s, KBD12, LATCHED_PC, LATCHEDDATA,
       MQ, not_3_out, or_5_out, PCIN, RAMDATA, register_1_q, rotater_1_p4, xor_5_out;
  wire [15:0] KEYBOARD_d;
  wire [31:0] INSTRUCTION_COUNT_out;

  Comparator #(.Bits(12)) comparator_1 (.a({RA3, RA2, RA1, RA0}), .b(12'h5e), .eq(comparator_1_eq));  // open: gt, lt
  and and_1 (and_1_out, comparator_1_eq, RAM_WE);
  xor xor_1 (xor_1_out, CK0, PC_eq_200);
  Counter #(.Bits(32)) INSTRUCTION_COUNT (.en(1'b1), .C(CK0), .clr(1'b0), .out(INSTRUCTION_COUNT_out));  // open: ovf
  Register #(.Bits(12)) register_1 (.D(RAMDATA), .C(and_1_out), .en(1'b1), .Q(register_1_q));
  Register #(.Bits(12)) register_2 (.D(BUS_PC), .C(xor_1_out), .en(1'b1), .Q(LATCHED_PC));
  COUNTER counter_1 (
    .i1(CNT_AND), .i2(CNT_AND_I), .i3(CNT_AND_IA), .i4(CNT_TAD), .i5(CNT_TAD_I), .i6(CNT_TAD_IA),
    .i7(CNT_ISZ), .i8(CNT_ISZ_I), .i9(CNT_ISZ_IA), .i10(CNT_DCA), .i11(CNT_DCA_I), .i12(CNT_DCA_IA),
    .i13(CNT_JMS), .i14(CNT_JMS_I), .i15(CNT_JMS_IA), .i16(CNT_JMP), .i17(CNT_JMP_I), .i18(CNT_JMP_IA),
    .i19(CNT_OPR1), .i20(CNT_OPR2), .i21(IOT_DEVCPU), .i22(IOT_DEVHSR), .i23(IOT_DEVHSP), .i24(IOT_DEVKBD),
    .i25(IOT_DEVPRI), .i26(IOT_DEV5), .i27(IOT_DEV6), .i28(IOT_DEV7), .i29(IOT_DEV8), .i30(IOT_DEV9),
    .i31(IOT_DEV1x), .i32(IOT_DEV2x), .C(1'b0), .E(1'b1), .o1(counter_1_o1), .o2(counter_1_o2),
    .o3(counter_1_o3), .o4(counter_1_o4), .o5(counter_1_o5), .o6(counter_1_o6), .o7(counter_1_o7),
    .o8(counter_1_o8), .o9(counter_1_o9), .o10(counter_1_o10), .o11(counter_1_o11), .o12(counter_1_o12),
    .o13(counter_1_o13), .o14(counter_1_o14), .o15(counter_1_o15), .o16(counter_1_o16), .o17(counter_1_o17),
    .o18(counter_1_o18), .o19(counter_1_o19), .o20(counter_1_o20), .o21(counter_1_o21), .o22(counter_1_o22),
    .o23(counter_1_o23), .o24(counter_1_o24), .o25(counter_1_o25), .o26(counter_1_o26), .o27(counter_1_o27),
    .o28(counter_1_o28), .o29(counter_1_o29), .o30(counter_1_o30), .o31(counter_1_o31), .o32(counter_1_o32));
  AUTOCAPTURE autocapture_1 (
    .D(RAMDATA), .A({RA3, RA2, RA1, RA0}), .WR(RAM_WE), ._10(autocapture_1__10), ._11(autocapture_1__11),
    ._12(autocapture_1__12), ._13(autocapture_1__13), ._14(autocapture_1__14), ._15(autocapture_1__15),
    ._16(autocapture_1__16), ._17(autocapture_1__17));
  // Probe on INSTRUCTION_COUNT_out
  // Probe on register_1_q
  // Probe on counter_1_o1
  // Probe on counter_1_o2
  // Probe on counter_1_o3
  // Probe on counter_1_o4
  // Probe on counter_1_o5
  // Probe on counter_1_o6
  // Probe on counter_1_o7
  // Probe on counter_1_o8
  // Probe on counter_1_o9
  // Probe on counter_1_o10
  // Probe on counter_1_o11
  // Probe on counter_1_o12
  // Probe on counter_1_o13
  // Probe on counter_1_o14
  // Probe on counter_1_o15
  // Probe on counter_1_o16
  // Probe on counter_1_o17
  // Probe on counter_1_o18
  // Probe on counter_1_o19
  // Probe on counter_1_o20
  // Probe on counter_1_o21
  // Probe on counter_1_o22
  // Probe on counter_1_o23
  // Probe on counter_1_o24
  // Probe on counter_1_o25
  // Probe on counter_1_o26
  // Probe on counter_1_o27
  // Probe on counter_1_o28
  // Probe on counter_1_o29
  // Probe on counter_1_o30
  // Probe on counter_1_o31
  // Probe on counter_1_o32
  // Probe on autocapture_1__10
  // Probe on autocapture_1__11
  // Probe on autocapture_1__12
  // Probe on autocapture_1__13
  // Probe on autocapture_1__14
  // Probe on autocapture_1__15
  // Probe on autocapture_1__16
  // Probe on autocapture_1__17
  assign PCIN = PC_eq_200 ? 12'h80 : 12'bz;  // Driver driver_1
  assign driver_2_out = PC_eq_200 ? PC_eq_200 : 1'bz;  // Driver driver_2
  assign PC_LD = PC_eq_200 ? PC_eq_200 : 1'bz;  // Driver driver_3
  Seven_Seg_Hex seven_seg_hex_1 (.d({1'b0, BUS_PC[11:9]}), .dp(1'b0));
  Seven_Seg_Hex seven_seg_hex_2 (.d({1'b0, BUS_IR[11:9]}), .dp(1'b0));
  Seven_Seg_Hex seven_seg_hex_3 (.d({1'b0, AC[11:9]}), .dp(1'b0));
  Seven_Seg_Hex seven_seg_hex_4 (.d({1'b0, MQ[11:9]}), .dp(1'b0));
  LED led_1 (.in(LINK));
  Seven_Seg_Hex seven_seg_hex_5 (.d({1'b0, IND3}), .dp(1'b0));
  Seven_Seg_Hex seven_seg_hex_6 (.d({1'b0, RA3}), .dp(1'b0));
  Seven_Seg_Hex seven_seg_hex_7 (.d({1'b0, RAMDATA[11:9]}), .dp(1'b0));
  Seven_Seg_Hex seven_seg_hex_8 (.d({1'b0, PCIN[11:9]}), .dp(1'b0));
  Seven_Seg_Hex seven_seg_hex_9 (.d({1'b0, DA3}), .dp(1'b0));
  // OC12 oc12_1: pin names not known; wires that end beside it: BUS_IR[6:0], BUS_PC[11:7], MP, IR2PC, PCIN[6:0], PCIN[11:7], PCIN
  LED led_2 (.in(IR2PC));
  Seven_Seg_Hex seven_seg_hex_10 (.d({1'b0, BUS_PC[8:6]}), .dp(1'b0));
  Seven_Seg_Hex seven_seg_hex_11 (.d({1'b0, BUS_IR[8:6]}), .dp(1'b0));
  Seven_Seg_Hex seven_seg_hex_12 (.d({1'b0, AC[8:6]}), .dp(1'b0));
  Seven_Seg_Hex seven_seg_hex_13 (.d({1'b0, MQ[8:6]}), .dp(1'b0));
  Seven_Seg_Hex seven_seg_hex_14 (.d({1'b0, IND2}), .dp(1'b0));
  Seven_Seg_Hex seven_seg_hex_15 (.d({1'b0, RA2}), .dp(1'b0));
  Seven_Seg_Hex seven_seg_hex_16 (.d({1'b0, RAMDATA[8:6]}), .dp(1'b0));
  Seven_Seg_Hex seven_seg_hex_17 (.d({1'b0, PCIN[8:6]}), .dp(1'b0));
  Seven_Seg_Hex seven_seg_hex_18 (.d({1'b0, DA2}), .dp(1'b0));
  Seven_Seg_Hex seven_seg_hex_19 (.d({1'b0, BUS_PC[5:3]}), .dp(1'b0));
  Seven_Seg_Hex seven_seg_hex_20 (.d({1'b0, BUS_IR[5:3]}), .dp(1'b0));
  Seven_Seg_Hex seven_seg_hex_21 (.d({1'b0, AC[5:3]}), .dp(1'b0));
  Seven_Seg_Hex seven_seg_hex_22 (.d({1'b0, MQ[5:3]}), .dp(1'b0));
  Seven_Seg_Hex seven_seg_hex_23 (.d({1'b0, IND1}), .dp(1'b0));
  Seven_Seg_Hex seven_seg_hex_24 (.d({1'b0, RA1}), .dp(1'b0));
  Seven_Seg_Hex seven_seg_hex_25 (.d({1'b0, RAMDATA[5:3]}), .dp(1'b0));
  Seven_Seg_Hex seven_seg_hex_26 (.d({1'b0, PCIN[5:3]}), .dp(1'b0));
  Seven_Seg_Hex seven_seg_hex_27 (.d({1'b0, DA1}), .dp(1'b0));
  // Probe on PCIN
  LED led_3 (.in(RAMD2PC));
  assign PCIN = RAMD2PC ? {DA3, DA2, DA1, DA0} : 12'bz;  // Driver driver_4
  LED led_4 (.in(IND2PC));
  assign PCIN = IND2PC ? {IND3, IND2, IND1, IND0} : 12'bz;  // Driver driver_5
  Seven_Seg_Hex seven_seg_hex_28 (.d({1'b0, BUS_PC[2:0]}), .dp(1'b0));
  Seven_Seg_Hex seven_seg_hex_29 (.d({1'b0, BUS_IR[2:0]}), .dp(1'b0));
  Seven_Seg_Hex seven_seg_hex_30 (.d({1'b0, AC[2:0]}), .dp(1'b0));
  Seven_Seg_Hex seven_seg_hex_31 (.d({1'b0, MQ[2:0]}), .dp(1'b0));
  Seven_Seg_Hex seven_seg_hex_32 (.d({1'b0, IND0}), .dp(1'b0));
  Seven_Seg_Hex seven_seg_hex_33 (.d({1'b0, RA0}), .dp(1'b0));
  Seven_Seg_Hex seven_seg_hex_34 (.d({1'b0, RAMDATA[2:0]}), .dp(1'b0));
  Seven_Seg_Hex seven_seg_hex_35 (.d({1'b0, PCIN[2:0]}), .dp(1'b0));
  Seven_Seg_Hex seven_seg_hex_36 (.d({1'b0, DA0}), .dp(1'b0));
  LED led_5 (.in(PC_CK));
  xor xor_2 (xor_2_out, PC_CK, driver_2_out);
  // Probe on {DA3, DA2, DA1, DA0}
  not not_1 (not_1_out, xor_2_out);
  LED led_6 (.in(PC_LD));
  LED led_7 (.in(RAMD2AC_ADD));
  CounterPreset #(.Bits(12)) PC (
    .en(1'b1), .C(not_1_out), .dir(1'b0), .in(PCIN), .ld(PC_LD), .clr(reset_1_out), .out(BUS_PC));  // open: ovf
  LED led_8 (.in(L_SKON));
  LED led_9 (.in(L_ION));
  LED led_10 (.in(i_nop));
  LED led_11 (.in(AND));
  LED led_12 (.in(TAD));
  assign and_2_out = AC & {DA3, DA2, DA1, DA0};  // And and_2, 12 bits wide
  Add #(.Bits(12)) add_1 (.a(AC), .b({DA3, DA2, DA1, DA0}), .c_i(1'b0), .s(add_1_s), .c_o(add_1_c_o));
  and and_3 (and_3_out, add_1_c_o, RAMD2AC_ADD);
  LED led_13 (.in(and_3_out));
  Reset #(.invertOutput("false")) reset_1 (.out(reset_1_out));
  LED led_14 (.in(L_IOF));
  LED led_15 (.in(i_cla));
  LED led_16 (.in(i_cll));
  LED led_17 (.in(ISZ));
  // Probe on AC
  // Probe on and_2_out
  // Probe on add_1_s
  LED led_18 (.in(add_1_c_o));
  // Probe on rotater_1_p4
  D_FF TAD_OVF (.D(and_3_out), .C(STB1), .Q(TAD_OVF_q));  // open: nQ
  LED led_19 (.in(STB1));
  // Probe on BUS_PC
  LED led_20 (.in(L_SRQ));
  LED led_21 (.in(i_cma));
  LED led_22 (.in(DCA));
  Button S (.out(S_out));
  Button I (.out(I_out));
  Button R (.out(R_out));
  Button H (.out(H_out));
  Button P (.out(PC_eq_200));
  LED led_23 (.in(MQ_CK));
  LED led_24 (.in(TAD_OVF_q));
  // OC12 oc12_2: pin names not known; wires that end beside it: BUS_PC, BUS_IR[6:0], BUS_PC[11:7], MP, IR2RAMA, {RA2[0], RA1, RA0}, {RA3, RA2[2:1]}
  LED led_25 (.in(IR2RAMA));
  LED led_26 (.in(L_GTF));
  LED led_27 (.in(L_RTF));
  LED led_28 (.in(i_cml));
  LED led_29 (.in(JMS));
  LED led_30 (.in(JMP));
  Monoflop #(.timerDelay(2)) monoflop_1 (.C(I_out), .R(1'b0), .Q(monoflop_1_q));  // open: nQ
  Monoflop monoflop_2 (.C(R_out), .R(1'b0), .Q(monoflop_2_q));  // open: nQ
  and and_4 (and_4_out, OPR_MQL, MQ_CK);
  assign driver_6_out = RAMD2AC_AND ? and_2_out : 12'bz;  // Driver driver_6
  LED led_31 (.in(RAMD2AC_AND));
  assign driver_6_out = RAMD2AC_ADD ? add_1_s : 12'bz;  // Driver driver_7
  LED led_32 (.in(RAMD2AC_ADD));
  assign driver_6_out = ROT2AC ? rotater_1_p4 : 12'bz;  // Driver driver_8
  LED led_33 (.in(ROT2AC));
  xor xor_3 (xor_3_out, TAD_OVF_q, rotater_1_p5);
  LED led_34 (.in(PC2ADDR));
  assign {RA3, RA2, RA1, RA0} = PC2ADDR ? BUS_PC : 12'bz;  // Driver driver_9
  LED led_35 (.in(L_SGT));
  LED led_36 (.in(i_iac));
  LED led_37 (.in(IOT));
  Switch #(.Closed("true")) HLT_ENABLED (.A(HALT), .B(HLT_ENABLED_b));
  Comparator #(.Bits(12)) comparator_2 (.a(BUS_PC), .b({12{1'b1}}), .eq(comparator_2_eq));  // open: gt, lt
  // Probe on and_5_out
  LED led_38 (.in(and_4_out));
  // Probe on driver_6_out
  LED led_39 (.in(xor_3_out));
  // Probe on {RA3, RA2, RA1, RA0}
  LED led_40 (.in(IND2RAMA));
  LED led_41 (.in(L_CAF));
  LED led_42 (.in(i_rar));
  LED led_43 (.in(OPR));
  RS_FF_AS rs_ff_as_1 (.S(monoflop_2_q), .R(or_3_out), .Q(rs_ff_as_1_q));  // open: nQ
  PullDown pulldown_1 (.out(HLT_ENABLED_b));
  Switch #(.Closed("true")) BP_ENABLED (.A(comparator_2_eq), .B(BP_ENABLED_b));
  assign and_5_out = AC & ~bitextender_1_out;  // And and_5, 12 bits wide
  LED led_44 (.in(AC_CK));
  D_FF u_LINK (.D(xor_3_out), .C(LINK_CK), .Q(LINK));  // open: nQ
  LED led_45 (.in(LINK_CK));
  LED led_46 (.in(RAM_WE));
  LED led_47 (.in(RAM_OE));
  assign {RA3, RA2, RA1, RA0} = IND2RAMA ? {IND3, IND2, IND1, IND0} : 12'bz;  // Driver driver_10
  LED led_48 (.in(L_KCF));
  LED led_49 (.in(i_rtr));
  LED led_50 (.in(NOIND));
  or or_1 (or_1_out, monoflop_1_q, monoflop_2_q, rs_ff_as_1_q);
  D_FF #(.Bits(12)) u_MQ (.D(and_5_out), .C(and_4_out), .Q(MQ));  // open: nQ
  D_FF #(.Bits(12)) u_AC (.D(driver_6_out), .C(AC_CK), .Q(AC));  // open: nQ
  or or_2 (or_2_out, OPR_CLA1, OPR_CLA2, OPR_CLA3, OPR_MQL, CLA, CLA_KCC);
  LED led_51 (.in(LINK));
  EEPROM #(.AddrBits(17), .isProgramMemory("true"), .Bits(12)) eeprom_1 (
    .A({{5{1'b0}}, RA3, RA2, RA1, RA0}), .CS(1'b1), .WE(RAM_WE), .OE(RAM_OE), .D(RAMDATA));
  LED led_52 (.in(L_KSF));
  LED led_53 (.in(i_ral));
  LED led_54 (.in(i_rtl));
  LED led_55 (.in(IND));
  LED led_56 (.in(or_1_out));
  or or_3 (or_3_out, H_out, BP_ENABLED_b, HLT_ENABLED_b);
  LED led_57 (.in(or_3_out));
  PullDown pulldown_2 (.out(BP_ENABLED_b));
  // Probe on MQ
  BitExtender #(.inputBits(1), .outputBits(12)) bitextender_1 (.in(OPR_CLA3), .out(bitextender_1_out));
  // Probe on AC
  BitExtender #(.inputBits(1), .outputBits(12)) bitextender_2 (.in(or_2_out), .out(bitextender_2_out));
  LED led_58 (.in(or_2_out));
  // Probe on RAMDATA
  LED led_59 (.in(L_KCC));
  LED led_60 (.in(i_skp));
  LED led_61 (.in(AUTOIND));
  assign and_6_out = AC & ~bitextender_2_out;  // And and_6, 12 bits wide
  or or_4 (or_4_out, CLL, OPR_CLL);
  LED led_62 (.in(OPR_CLL));
  assign {DA3, DA2, DA1, DA0} = RAM_OE ? RAMDATA : 12'bz;  // Driver driver_11
  assign RAMDATA = RAM_WE ? {DA3, DA2, DA1, DA0} : 12'bz;  // Driver driver_12
  LED led_63 (.in(L_KRS));
  LED led_64 (.in(L_KIE));
  LED led_65 (.in(i_sma));
  LED led_66 (.in(MP));
  D_FF d_ff_1 (.D(counter_2_ovf), .C(clk), .Q(d_ff_1_q));  // open: nQ
  // Probe on and_6_out
  and and_7 (and_7_out, LINK, ~or_4_out);  // And
  LED led_67 (.in(FORCE4000));
  assign {DA3, DA2, DA1, DA0} = FORCE4000 ? 12'h800 : 12'bz;  // Driver driver_13
  LED led_68 (.in(PC2RAMD));
  assign {DA3, DA2, DA1, DA0} = PC2RAMD ? BUS_PC : 12'bz;  // Driver driver_14
  LED led_69 (.in(L_KRB));
  LED led_70 (.in(i_sza));
  RS_FF_AS rs_ff_as_2 (.S(or_1_out), .R(d_ff_1_q), .Q(rs_ff_as_2_q));  // open: nQ
  assign driver_15_out = OPR_MQA ? MQ : 12'bz;  // Driver driver_15
  LED led_71 (.in(OPR_MQA));
  LED led_72 (.in(and_7_out));
  // Probe on {DA3, DA2, DA1, DA0}
  LED led_73 (.in(INC2RAMD));
  LED led_74 (.in(AC2RAMD));
  assign {DA3, DA2, DA1, DA0} = AC2RAMD ? AC : 12'bz;  // Driver driver_16
  LED led_75 (.in(i_sna));
  LED led_76 (.in(i_spa));
  and and_8 (and_8_out, rs_ff_as_2_q, clk);
  assign driver_15_out = OR_STATUS12 ? {LINK, 1'b0, IRQ_BUS, IRQ_INHIBIT, FLAG_GIE, {7{1'b0}}} : 12'bz;  // Driver driver_17
  LED led_77 (.in(OR_STATUS12));
  assign driver_15_out = OR_KBD12 ? KBD12 : 12'bz;  // Driver driver_18
  LED led_78 (.in(OR_KBD12));
  assign driver_15_out = OPR_OSR ? not_3_out : 12'bz;  // Driver driver_19
  LED led_79 (.in(OPR_OSR));
  // Probe on driver_15_out
  assign or_5_out = driver_15_out | and_6_out;  // Or or_5, 12 bits wide
  BitExtender #(.inputBits(1), .outputBits(12)) bitextender_3 (.in(OPR_CMA), .out(bitextender_3_out));
  LED led_80 (.in(OPR_CMA));
  or or_6 (or_6_out, RTF_LINK, OPR_CML);
  LED led_81 (.in(OPR_CML));
  not not_2 (not_2_out, IR_CK);
  LED led_82 (.in(IR_CK));
  assign {DA3, DA2, DA1, DA0} = INC2RAMD ? INC_s : 12'bz;  // Driver driver_20
  LED led_83 (.in(L_TFL));
  LED led_84 (.in(L_TSF));
  LED led_85 (.in(i_snl));
  or or_7 (or_7_out, S_out, and_8_out);
  // Probe on {LINK, 1'b0, IRQ_BUS, IRQ_INHIBIT, FLAG_GIE, {7{1'b0}}}
  // Probe on KBD12
  // Probe on not_3_out
  // Probe on or_5_out
  xor xor_4 (xor_4_out, and_7_out, or_6_out);
  // TRANSP_LATCH IR: pin names not known; wires that end beside it: {DA3, DA2, DA1, DA0}, {DA3, DA2, DA1, DA0}, not_2_out, BUS_IR, BUS_IR
  LED led_86 (.in(L_TCF));
  LED led_87 (.in(i_szl));
  LED led_88 (.in(or_7_out));
  assign xor_5_out = or_5_out ^ bitextender_3_out;  // XOr xor_5, 12 bits wide
  LED led_89 (.in(xor_4_out));
  // Probe on BUS_IR
  LED led_90 (.in(L_TPC));
  LED led_91 (.in(i_osr));
  Counter #(.Bits(5)) counter_2 (
    .en(1'b1), .C(or_7_out), .clr(counter_2_ovf), .out(counter_2_out), .ovf(counter_2_ovf));
  DipSwitch #(.dipDefault("true")) dipswitch_1 (.out(dipswitch_1_out[11]));
  assign not_3_out = ~dipswitch_1_out;  // Not not_3, 12 bits wide
  // Probe on xor_5_out
  LED led_92 (.in(OPR_IAC));
  xor xor_6 (xor_6_out, and_9_out, xor_4_out);
  D_FF #(.Bits(12)) u_IND (.D({DA3, DA2, DA1, DA0}), .C(IND_CK), .Q({IND3, IND2, IND1, IND0}));  // open: nQ
  LED led_93 (.in(IND_CK));
  LED led_94 (.in(L_TSK));
  LED led_95 (.in(L_TLS));
  LED led_96 (.in(i_hlt));
  DipSwitch #(.dipDefault("true")) dipswitch_2 (.out(dipswitch_1_out[10]));
  DipSwitch #(.dipDefault("true")) dipswitch_3 (.out(dipswitch_1_out[9]));
  DipSwitch #(.dipDefault("true")) dipswitch_4 (.out(dipswitch_1_out[8]));
  Add #(.Bits(12)) add_2 (.a(xor_5_out), .b({12{1'b0}}), .c_i(OPR_IAC), .s(add_2_s), .c_o(add_2_c_o));
  LED led_97 (.in(xor_6_out));
  SEQUENCER sequencer_1 (
    .PH_FIRST(PH_FIRST), .PH_STB(PH_STB), .PH_LAST(PH_LAST),
    .STB_bits({STB9, STB8, STB7, STB6, STB5, STB4, STB3, STB2, STB1, STB0}),
    .CK_bits({CK9, CK8, CK7, CK6, CK5, CK4, CK3, CK2, CK1, CK0}), .CK_num(CK_NUM), .IN(counter_2_out));
  DipSwitch #(.dipDefault("true")) dipswitch_5 (.out(dipswitch_1_out[7]));
  DipSwitch #(.dipDefault("true")) dipswitch_6 (.out(dipswitch_1_out[6]));
  DipSwitch #(.dipDefault("true")) dipswitch_7 (.out(dipswitch_1_out[5]));
  // Probe on add_2_s
  and and_9 (and_9_out, add_2_c_o, OPR_IAC);
  LED led_98 (.in(add_2_c_o));
  // Probe on {IND3, IND2, IND1, IND0}
  LED led_99 (.in(DATA_CK));
  Seven_Seg_Hex seven_seg_hex_37 (.d(CK_NUM), .dp(1'b0));
  LED led_100 (.in(PH_FIRST));
  DipSwitch #(.dipDefault("true")) dipswitch_8 (.out(dipswitch_1_out[4]));
  DipSwitch #(.dipDefault("true")) dipswitch_9 (.out(dipswitch_1_out[3]));
  DipSwitch #(.dipDefault("true")) dipswitch_10 (.out(dipswitch_1_out[2]));
  LED led_101 (.in(and_9_out));
  D_FF #(.Bits(12)) DATA (.D({DA3, DA2, DA1, DA0}), .C(DATA_CK), .Q(LATCHEDDATA));  // open: nQ
  LED led_102 (.in(PH_STB));
  LED led_103 (.in(PH_LAST));
  DipSwitch #(.dipDefault("true")) dipswitch_11 (.out(dipswitch_1_out[1]));
  DipSwitch #(.dipDefault("true")) dipswitch_12 (.out(dipswitch_1_out[0]));
  // Probe on LATCHEDDATA
  Seven_Seg_Hex seven_seg_hex_38 (.d(CK_NUM), .dp(1'b0));
  // ROTATER rotater_1: pin names not known; wires that end beside it: {OPR_RIGHT, OPR_LEFT, OPR_X2}, add_2_s, xor_6_out, rotater_1_p4, rotater_1_p5
  LED led_104 (.in(IND2INC));
  assign driver_21_out = IND2INC ? {IND3, IND2, IND1, IND0} : 12'bz;  // Driver driver_21
  LED led_105 (.in(LD2INC));
  assign driver_21_out = LD2INC ? LATCHEDDATA : 12'bz;  // Driver driver_22
  // Probe on LATCHED_PC
  // Probe on rotater_1_p4
  Seven_Seg_Hex seven_seg_hex_39 (.d(CK_NUM), .dp(1'b0));
  LED led_106 (.in(PH_FIRST));
  LED led_107 (.in(PH_STB));
  // Probe on INC_s
  // Probe on driver_21_out
  LED led_108 (.in(PH_FIRST));
  LED led_109 (.in(PH_STB));
  LED led_110 (.in(PH_LAST));
  Add #(.Bits(12)) INC (.a({12{1'b0}}), .b(driver_21_out), .c_i(1'b1), .s(INC_s), .c_o(INCZERO));
  LED led_111 (.in(PH_LAST));
  nor nor_1 (nor_1_out, AC[0], AC[1], AC[2], AC[3], AC[4], AC[5], AC[6], AC[7], AC[8], AC[9], AC[10], AC[11]);
  LED led_112 (.in(nor_1_out));
  and and_10 (and_10_out, nor_1_out, OPR_SZASNA);
  and and_11 (and_11_out, AC[11], OPR_SMASPA);
  and and_12 (and_12_out, LINK, OPR_SNLSZL);
  and and_13 (CNT_AND, AND, NOIND, CK1);
  LED led_113 (.in(CNT_AND));
  and and_14 (and_14_out, AND, NOIND, STB1);
  LED led_114 (.in(and_14_out));
  LED led_115 (.in(and_10_out));
  LED led_116 (.in(and_11_out));
  LED led_117 (.in(and_12_out));
  assign IR2RAMA = CNT_AND ? CNT_AND : 1'bz;  // Driver driver_23
  assign RAMD2AC_AND = CNT_AND ? CNT_AND : 1'bz;  // Driver driver_24
  assign RAM_OE = CNT_AND ? CNT_AND : 1'bz;  // Driver driver_25
  assign AC_CK = and_14_out ? and_14_out : 1'bz;  // Driver driver_26
  or or_8 (or_8_out, and_10_out, and_11_out, and_12_out);
  xor xor_7 (SKIP, or_8_out, OPR_TSTINV);
  LED led_118 (.in(or_8_out));
  and and_15 (HALT, OPR_HLT, CK1);
  LED led_119 (.in(SKIP));
  LED led_120 (.in(HALT));
  and and_16 (CNT_AND_I, AND, IND, CK1);
  and and_17 (and_17_out, IND, AND, STB1);
  and and_18 (and_18_out, IND, AND, CK2);
  and and_19 (and_19_out, IND, AND, STB2);
  assign IR2RAMA = CNT_AND_I ? CNT_AND_I : 1'bz;  // Driver driver_27
  LED led_121 (.in(CNT_AND_I));
  assign RAMD2IND = CNT_AND_I ? CNT_AND_I : 1'bz;  // Driver driver_28
  assign RAM_OE = CNT_AND_I ? CNT_AND_I : 1'bz;  // Driver driver_29
  LED led_122 (.in(and_17_out));
  assign IND_CK = and_17_out ? and_17_out : 1'bz;  // Driver driver_30
  assign IND2RAMA = and_18_out ? and_18_out : 1'bz;  // Driver driver_31
  LED led_123 (.in(and_18_out));
  assign RAMD2AC_AND = and_18_out ? and_18_out : 1'bz;  // Driver driver_32
  assign RAM_OE = and_18_out ? and_18_out : 1'bz;  // Driver driver_33
  LED led_124 (.in(and_19_out));
  assign AC_CK = and_19_out ? and_19_out : 1'bz;  // Driver driver_34
  and and_20 (and_20_out, IRQ_BUS, FLAG_GIE);
  LED led_125 (.in(and_20_out));
  and and_21 (and_21_out, CK0, ~and_20_out);  // And
  and and_22 (and_22_out, CK0, and_20_out);
  LED led_126 (.in(and_21_out));
  LED led_127 (.in(and_22_out));
  assign PC2ADDR = and_21_out ? and_21_out : 1'bz;  // Driver driver_35
  assign RAM_OE = and_21_out ? and_21_out : 1'bz;  // Driver driver_36
  assign IR_CK = and_21_out ? and_21_out : 1'bz;  // Driver driver_37
  assign PC_CK = and_21_out ? and_21_out : 1'bz;  // Driver driver_38
  assign IRQ_JMS = and_22_out ? and_22_out : 1'bz;  // Driver driver_39
  assign FORCE4000 = and_22_out ? and_22_out : 1'bz;  // Driver driver_40
  assign IR_CK = and_22_out ? and_22_out : 1'bz;  // Driver driver_41
  and and_23 (and_23_out, AND, AUTOIND, CK4);
  and and_24 (and_24_out, AND, AUTOIND, STB4);
  and and_25 (CNT_AND_IA, AND, AUTOIND, CK1);
  and and_26 (and_26_out, AND, AUTOIND, STB1);
  and and_27 (and_27_out, AND, AUTOIND, CK2);
  and and_28 (and_28_out, AND, AUTOIND, STB2);
  and and_29 (and_29_out, AND, AUTOIND, CK3);
  LED led_128 (.in(and_29_out));
  and and_30 (and_30_out, AND, AUTOIND, STB3);
  LED led_129 (.in(and_30_out));
  LED led_130 (.in(and_23_out));
  LED led_131 (.in(and_24_out));
  assign IR2RAMA = CNT_AND_IA ? CNT_AND_IA : 1'bz;  // Driver driver_42
  LED led_132 (.in(CNT_AND_IA));
  assign RAM_OE = CNT_AND_IA ? CNT_AND_IA : 1'bz;  // Driver driver_43
  assign IND2INC = CNT_AND_IA ? CNT_AND_IA : 1'bz;  // Driver driver_44
  LED led_133 (.in(and_26_out));
  assign IND_CK = and_26_out ? and_26_out : 1'bz;  // Driver driver_45
  assign INC2RAMD = and_27_out ? and_27_out : 1'bz;  // Driver driver_46
  LED led_134 (.in(and_27_out));
  assign IND2INC = and_27_out ? and_27_out : 1'bz;  // Driver driver_47
  assign IR2RAMA = and_27_out ? and_27_out : 1'bz;  // Driver driver_48
  LED led_135 (.in(and_28_out));
  assign RAM_WE = and_28_out ? and_28_out : 1'bz;  // Driver driver_49
  assign IR2RAMA = and_29_out ? and_29_out : 1'bz;  // Driver driver_50
  assign RAMD2IND = and_29_out ? and_29_out : 1'bz;  // Driver driver_51
  assign RAM_OE = and_29_out ? and_29_out : 1'bz;  // Driver driver_52
  assign IND_CK = and_30_out ? and_30_out : 1'bz;  // Driver driver_53
  assign IND2RAMA = and_23_out ? and_23_out : 1'bz;  // Driver driver_54
  assign RAMD2AC_AND = and_23_out ? and_23_out : 1'bz;  // Driver driver_55
  assign RAM_OE = and_23_out ? and_23_out : 1'bz;  // Driver driver_56
  assign AC_CK = and_24_out ? and_24_out : 1'bz;  // Driver driver_57
  Keyboard KEYBOARD (.C(clk), .en(KEYBOARD_av), .D(KEYBOARD_d), .av(KEYBOARD_av));
  // Probe on KEYBOARD_d[11:0]
  and and_31 (CNT_TAD, TAD, NOIND, CK1);
  and and_32 (and_32_out, NOIND, TAD, STB1);
  or or_9 (or_9_out, IOT_ION, RTF_ION);
  Register #(.Bits(12)) register_3 (.D(KEYBOARD_d[11:0]), .C(clk), .en(KEYBOARD_av), .Q(KBD12));
  or or_10 (or_10_out, KEYBOARD_av, 1'b0, 1'b0, 1'b0, 1'b0);
  or or_11 (or_11_out, IOT_KCF, IOT_KCC, IOT_KRB, 1'b0, 1'b0);
  and and_33 (and_33_out, IOT_KCC, CK1);
  and and_34 (and_34_out, IOT_KCC, STB1);
  and and_35 (and_35_out, IOT_KSF, CK1, FLAG_KBD);
  and and_36 (and_36_out, IOT_KRS, CK1);
  and and_37 (and_37_out, IOT_KRS, STB1);
  and and_38 (and_38_out, IOT_KRB, CK1);
  and and_39 (and_39_out, IOT_KRB, STB1);
  and and_40 (and_40_out, IOT_KIE, AC[0]);
  and and_41 (and_41_out, IOT_KIE, ~AC[0]);  // And
  LED led_136 (.in(CNT_TAD));
  LED led_137 (.in(and_32_out));
  and and_42 (and_42_out, CK1, or_9_out);
  LED led_138 (.in(or_9_out));
  and and_43 (and_43_out, IOT_CAF, CK1);
  LED led_139 (.in(and_43_out));
  and and_44 (and_44_out, IOT_CAF, STB1);
  LED led_140 (.in(and_44_out));
  and and_45 (and_45_out, IOT_SKON, FLAG_GIE, CK1);
  LED led_141 (.in(and_45_out));
  and and_46 (and_46_out, IOT_SKON, FLAG_GIE, STB1);
  LED led_142 (.in(and_46_out));
  and and_47 (and_47_out, FLAG_KBDIE, FLAG_PRN);
  LED led_143 (.in(and_47_out));
  and and_48 (and_48_out, FLAG_KBDIE, FLAG_KBD);
  LED led_144 (.in(and_48_out));
  // Probe on KBD12
  LED led_145 (.in(or_10_out));
  RS_FF_AS KBD (.S(or_10_out), .R(or_11_out), .Q(FLAG_KBD));  // open: nQ
  LED led_146 (.in(or_11_out));
  LED led_147 (.in(and_33_out));
  assign ROT2AC = and_33_out ? and_33_out : 1'bz;  // Driver driver_58
  assign CLA_KCC = and_33_out ? and_33_out : 1'bz;  // Driver driver_59
  LED led_148 (.in(and_34_out));
  assign AC_CK = and_34_out ? and_34_out : 1'bz;  // Driver driver_60
  LED led_149 (.in(and_35_out));
  assign PC_CK = and_35_out ? and_35_out : 1'bz;  // Driver driver_61
  LED led_150 (.in(and_36_out));
  assign ROT2AC = and_36_out ? and_36_out : 1'bz;  // Driver driver_62
  assign OR_KBD12 = and_36_out ? and_36_out : 1'bz;  // Driver driver_63
  LED led_151 (.in(and_37_out));
  assign AC_CK = and_37_out ? and_37_out : 1'bz;  // Driver driver_64
  LED led_152 (.in(and_38_out));
  assign ROT2AC = and_38_out ? and_38_out : 1'bz;  // Driver driver_65
  assign OR_KBD12 = and_38_out ? and_38_out : 1'bz;  // Driver driver_66
  assign CLA_KCC = and_38_out ? and_38_out : 1'bz;  // Driver driver_67
  LED led_153 (.in(and_39_out));
  assign AC_CK = and_39_out ? and_39_out : 1'bz;  // Driver driver_68
  LED led_154 (.in(and_40_out));
  LED led_155 (.in(and_41_out));
  assign IR2RAMA = CNT_TAD ? CNT_TAD : 1'bz;  // Driver driver_69
  assign RAMD2AC_ADD = CNT_TAD ? CNT_TAD : 1'bz;  // Driver driver_70
  assign RAM_OE = CNT_TAD ? CNT_TAD : 1'bz;  // Driver driver_71
  assign AC_CK = and_32_out ? and_32_out : 1'bz;  // Driver driver_72
  assign LINK_CK = and_32_out ? and_32_out : 1'bz;  // Driver driver_73
  LED led_156 (.in(and_42_out));
  assign CLL = and_43_out ? and_43_out : 1'bz;  // Driver driver_74
  assign CLA = and_43_out ? and_43_out : 1'bz;  // Driver driver_75
  assign ROT2AC = and_43_out ? and_43_out : 1'bz;  // Driver driver_76
  assign AC_CK = and_44_out ? and_44_out : 1'bz;  // Driver driver_77
  assign LINK_CK = and_44_out ? and_44_out : 1'bz;  // Driver driver_78
  assign PC_CK = and_45_out ? and_45_out : 1'bz;  // Driver driver_79
  LED led_157 (.in(FLAG_KBD));
  or or_12 (or_12_out, and_40_out, IOT_CAF);
  D_FF_AS d_ff_as_1 (.Set(1'b0), .D(and_42_out), .C(STB1), .Clr(IOT_IOF), .Q(IRQ_INHIBIT));  // open: nQ
  or or_13 (IRQ_BUS, and_47_out, and_48_out, 1'b0, 1'b0, 1'b0);
  RS_FF_AS KBD_IE (.S(or_12_out), .R(and_41_out), .Q(FLAG_KBDIE));  // open: nQ
  or or_14 (or_14_out, IOT_IOF, RTF_IOF, IRQ_JMS, IOT_CAF, and_46_out);
  and and_49 (and_49_out, IOT_SRQ, CK1, IRQ_BUS);
  LED led_158 (.in(IRQ_BUS));
  LED led_159 (.in(FLAG_KBDIE));
  D_FF_AS d_ff_as_2 (.Set(1'b0), .D(IRQ_INHIBIT), .C(STB1), .Clr(IOT_IOF), .Q(d_ff_as_2_q));  // open: nQ
  LED led_160 (.in(or_14_out));
  LED led_161 (.in(and_49_out));
  and and_50 (CNT_TAD_I, TAD, IND, CK1);
  and and_51 (and_51_out, TAD, IND, STB1);
  and and_52 (and_52_out, TAD, IND, CK2);
  and and_53 (and_53_out, TAD, IND, STB2);
  RS_FF_AS GIE (.S(d_ff_as_2_q), .R(or_14_out), .Q(FLAG_GIE));  // open: nQ
  assign PC_CK = and_49_out ? and_49_out : 1'bz;  // Driver driver_80
  LED led_162 (.in(CNT_TAD_I));
  LED led_163 (.in(and_51_out));
  assign IND2RAMA = and_52_out ? and_52_out : 1'bz;  // Driver driver_81
  LED led_164 (.in(and_52_out));
  assign RAMD2AC_ADD = and_52_out ? and_52_out : 1'bz;  // Driver driver_82
  assign RAM_OE = and_52_out ? and_52_out : 1'bz;  // Driver driver_83
  LED led_165 (.in(and_53_out));
  assign AC_CK = and_53_out ? and_53_out : 1'bz;  // Driver driver_84
  assign LINK_CK = and_53_out ? and_53_out : 1'bz;  // Driver driver_85
  LED led_166 (.in(FLAG_GIE));
  assign IR2RAMA = CNT_TAD_I ? CNT_TAD_I : 1'bz;  // Driver driver_86
  assign RAMD2IND = CNT_TAD_I ? CNT_TAD_I : 1'bz;  // Driver driver_87
  assign RAM_OE = CNT_TAD_I ? CNT_TAD_I : 1'bz;  // Driver driver_88
  assign IND_CK = and_51_out ? and_51_out : 1'bz;  // Driver driver_89
  Seven_Seg_Hex seven_seg_hex_40 (.d(CK_NUM), .dp(1'b0));
  // Probe on LATCHED_PC
  LED led_167 (.in(LINK));
  LED led_168 (.in(PH_FIRST));
  LED led_169 (.in(PH_STB));
  // Probe on AC
  or or_15 (or_15_out, IOT_TPC, IOT_TLS);
  LED led_170 (.in(or_15_out));
  and and_54 (and_54_out, IOT_GTF, CK2);
  and and_55 (and_55_out, IOT_GTF, STB2);
  LED led_171 (.in(PH_LAST));
  LED led_172 (.in(and_54_out));
  LED led_173 (.in(and_55_out));
  Terminal #(.termWidth(80), .termHeight(24)) PRINTER (.D({1'b0, AC[6:0]}), .C(or_15_out), .en(1'b1));
  and and_56 (CNT_TAD_IA, TAD, AUTOIND, CK1);
  and and_57 (and_57_out, TAD, AUTOIND, STB1);
  and and_58 (and_58_out, TAD, AUTOIND, CK2);
  and and_59 (and_59_out, TAD, AUTOIND, STB2);
  and and_60 (and_60_out, TAD, AUTOIND, CK3);
  and and_61 (and_61_out, TAD, AUTOIND, STB3);
  and and_62 (and_62_out, TAD, AUTOIND, CK4);
  LED led_174 (.in(and_62_out));
  and and_63 (and_63_out, TAD, AUTOIND, STB4);
  LED led_175 (.in(and_63_out));
  assign ROT2AC = and_54_out ? and_54_out : 1'bz;  // Driver driver_90
  assign CLA_KCC = and_54_out ? and_54_out : 1'bz;  // Driver driver_91
  assign OR_STATUS12 = and_54_out ? and_54_out : 1'bz;  // Driver driver_92
  assign AC_CK = and_55_out ? and_55_out : 1'bz;  // Driver driver_93
  Monoflop #(.timerDelay(50)) monoflop_3 (.C(or_15_out), .R(1'b0), .nQ(monoflop_3_nq));  // open: Q
  Monoflop #(.timerDelay(51)) monoflop_4 (.C(or_15_out), .R(1'b0), .Q(monoflop_4_q));  // open: nQ
  or or_16 (or_16_out, FLAG_PRN, FLAG_KBD);
  LED led_176 (.in(CNT_TAD_IA));
  LED led_177 (.in(and_57_out));
  LED led_178 (.in(and_58_out));
  LED led_179 (.in(and_59_out));
  assign IR2RAMA = and_60_out ? and_60_out : 1'bz;  // Driver driver_94
  LED led_180 (.in(and_60_out));
  assign RAMD2IND = and_60_out ? and_60_out : 1'bz;  // Driver driver_95
  assign RAM_OE = and_60_out ? and_60_out : 1'bz;  // Driver driver_96
  LED led_181 (.in(and_61_out));
  assign IND_CK = and_61_out ? and_61_out : 1'bz;  // Driver driver_97
  assign IND2RAMA = and_62_out ? and_62_out : 1'bz;  // Driver driver_98
  assign RAMD2AC_ADD = and_62_out ? and_62_out : 1'bz;  // Driver driver_99
  assign RAM_OE = and_62_out ? and_62_out : 1'bz;  // Driver driver_100
  assign AC_CK = and_63_out ? and_63_out : 1'bz;  // Driver driver_101
  assign LINK_CK = and_63_out ? and_63_out : 1'bz;  // Driver driver_102
  and and_64 (and_64_out, monoflop_3_nq, monoflop_4_q);
  or or_17 (or_17_out, and_64_out, IOT_TFL, 1'b0, 1'b0, 1'b0);
  or or_18 (or_18_out, IOT_TCF, IOT_CAF, IOT_TLS, 1'b0, 1'b0);
  and and_65 (and_65_out, IOT_TSF, CK1, FLAG_PRN);
  and and_66 (and_66_out, IOT_TSK, CK1, or_16_out);
  assign IR2RAMA = CNT_TAD_IA ? CNT_TAD_IA : 1'bz;  // Driver driver_103
  assign RAM_OE = CNT_TAD_IA ? CNT_TAD_IA : 1'bz;  // Driver driver_104
  assign IND2INC = CNT_TAD_IA ? CNT_TAD_IA : 1'bz;  // Driver driver_105
  assign IND_CK = and_57_out ? and_57_out : 1'bz;  // Driver driver_106
  assign INC2RAMD = and_58_out ? and_58_out : 1'bz;  // Driver driver_107
  assign IND2INC = and_58_out ? and_58_out : 1'bz;  // Driver driver_108
  assign IR2RAMA = and_58_out ? and_58_out : 1'bz;  // Driver driver_109
  assign RAM_WE = and_59_out ? and_59_out : 1'bz;  // Driver driver_110
  and and_67 (RTF_IOF, IOT_RTF, CK1, AC[7]);
  and and_68 (RTF_ION, IOT_RTF, CK1, ~AC[7]);  // And
  and and_69 (and_69_out, IOT_RTF, CK1);
  and and_70 (and_70_out, IOT_RTF, STB1);
  and and_71 (RTF_LINK, IOT_RTF, AC[11]);
  LED led_182 (.in(or_17_out));
  RS_FF_AS PRN (.S(or_17_out), .R(or_18_out), .Q(FLAG_PRN));  // open: nQ
  LED led_183 (.in(or_18_out));
  LED led_184 (.in(and_65_out));
  LED led_185 (.in(and_66_out));
  // Probe on {LINK, 1'b0, IRQ_BUS, IRQ_INHIBIT, FLAG_GIE, {7{1'b0}}}
  LED led_186 (.in(RTF_IOF));
  LED led_187 (.in(RTF_ION));
  LED led_188 (.in(and_69_out));
  assign CLL = and_69_out ? and_69_out : 1'bz;  // Driver driver_111
  LED led_189 (.in(and_70_out));
  assign LINK_CK = and_70_out ? and_70_out : 1'bz;  // Driver driver_112
  LED led_190 (.in(RTF_LINK));
  LED led_191 (.in(FLAG_PRN));
  assign PC_CK = and_65_out ? and_65_out : 1'bz;  // Driver driver_113
  assign PC_CK = and_66_out ? and_66_out : 1'bz;  // Driver driver_114
  and and_72 (CNT_ISZ, ISZ, NOIND, CK1);
  and and_73 (and_73_out, ISZ, NOIND, STB1);
  and and_74 (and_74_out, ISZ, NOIND, CK2);
  and and_75 (and_75_out, ISZ, NOIND, CK3);
  and and_76 (and_76_out, ISZ, NOIND, INCZERO, CK4);
  LED led_192 (.in(CNT_ISZ));
  LED led_193 (.in(and_73_out));
  LED led_194 (.in(and_74_out));
  LED led_195 (.in(and_75_out));
  LED led_196 (.in(and_76_out));
  assign IR2RAMA = CNT_ISZ ? CNT_ISZ : 1'bz;  // Driver driver_115
  assign RAM_OE = CNT_ISZ ? CNT_ISZ : 1'bz;  // Driver driver_116
  assign DATA_CK = and_73_out ? and_73_out : 1'bz;  // Driver driver_117
  assign LD2INC = and_73_out ? and_73_out : 1'bz;  // Driver driver_118
  assign IR2RAMA = and_74_out ? and_74_out : 1'bz;  // Driver driver_119
  assign RAM_WE = and_74_out ? and_74_out : 1'bz;  // Driver driver_120
  assign INC2RAMD = and_74_out ? and_74_out : 1'bz;  // Driver driver_121
  assign LD2INC = and_74_out ? and_74_out : 1'bz;  // Driver driver_122
  assign IR2RAMA = and_75_out ? and_75_out : 1'bz;  // Driver driver_123
  assign RAM_OE = and_75_out ? and_75_out : 1'bz;  // Driver driver_124
  assign LD2INC = and_75_out ? and_75_out : 1'bz;  // Driver driver_125
  assign PC_CK = and_76_out ? and_76_out : 1'bz;  // Driver driver_126
  assign LD2INC = and_76_out ? and_76_out : 1'bz;  // Driver driver_127
  Seven_Seg_Hex seven_seg_hex_41 (.d(CK_NUM), .dp(1'b0));
  // Probe on LATCHED_PC
  LED led_197 (.in(PH_FIRST));
  LED led_198 (.in(PH_STB));
  LED led_199 (.in(PH_LAST));
  and and_77 (CNT_ISZ_I, ISZ, IND, CK1);
  LED led_200 (.in(CNT_ISZ_I));
  and and_78 (and_78_out, ISZ, IND, STB1);
  LED led_201 (.in(and_78_out));
  and and_79 (and_79_out, ISZ, IND, CK2);
  LED led_202 (.in(and_79_out));
  and and_80 (and_80_out, ISZ, IND, STB2);
  LED led_203 (.in(and_80_out));
  and and_81 (and_81_out, ISZ, IND, CK3);
  LED led_204 (.in(and_81_out));
  and and_82 (and_82_out, ISZ, IND, CK4);
  LED led_205 (.in(and_82_out));
  and and_83 (and_83_out, ISZ, IND, INCZERO, CK5);
  LED led_206 (.in(and_83_out));
  assign IR2RAMA = CNT_ISZ_I ? CNT_ISZ_I : 1'bz;  // Driver driver_128
  assign RAMD2IND = CNT_ISZ_I ? CNT_ISZ_I : 1'bz;  // Driver driver_129
  assign RAM_OE = CNT_ISZ_I ? CNT_ISZ_I : 1'bz;  // Driver driver_130
  assign IND_CK = and_78_out ? and_78_out : 1'bz;  // Driver driver_131
  assign IND2RAMA = and_79_out ? and_79_out : 1'bz;  // Driver driver_132
  assign RAM_OE = and_79_out ? and_79_out : 1'bz;  // Driver driver_133
  assign DATA_CK = and_80_out ? and_80_out : 1'bz;  // Driver driver_134
  assign LD2INC = and_80_out ? and_80_out : 1'bz;  // Driver driver_135
  assign IND2RAMA = and_81_out ? and_81_out : 1'bz;  // Driver driver_136
  assign RAM_WE = and_81_out ? and_81_out : 1'bz;  // Driver driver_137
  assign INC2RAMD = and_81_out ? and_81_out : 1'bz;  // Driver driver_138
  assign LD2INC = and_81_out ? and_81_out : 1'bz;  // Driver driver_139
  assign IND2RAMA = and_82_out ? and_82_out : 1'bz;  // Driver driver_140
  assign RAM_OE = and_82_out ? and_82_out : 1'bz;  // Driver driver_141
  assign LD2INC = and_82_out ? and_82_out : 1'bz;  // Driver driver_142
  assign PC_CK = and_83_out ? and_83_out : 1'bz;  // Driver driver_143
  assign LD2INC = and_83_out ? and_83_out : 1'bz;  // Driver driver_144
  and and_84 (and_84_out, ISZ, AUTOIND, CK3);
  and and_85 (and_85_out, ISZ, AUTOIND, CK4);
  and and_86 (and_86_out, ISZ, AUTOIND, STB4);
  and and_87 (and_87_out, ISZ, AUTOIND, CK5);
  and and_88 (and_88_out, ISZ, AUTOIND, CK6);
  and and_89 (and_89_out, ISZ, AUTOIND, INCZERO, CK7);
  and and_90 (CNT_ISZ_IA, ISZ, AUTOIND, CK1);
  and and_91 (and_91_out, ISZ, AUTOIND, STB1);
  and and_92 (and_92_out, ISZ, AUTOIND, CK2);
  and and_93 (and_93_out, ISZ, AUTOIND, STB2);
  LED led_207 (.in(and_84_out));
  and and_94 (and_94_out, ISZ, AUTOIND, STB3);
  LED led_208 (.in(and_94_out));
  LED led_209 (.in(and_85_out));
  LED led_210 (.in(and_86_out));
  LED led_211 (.in(and_87_out));
  LED led_212 (.in(and_88_out));
  LED led_213 (.in(and_89_out));
  LED led_214 (.in(CNT_ISZ_IA));
  LED led_215 (.in(and_91_out));
  LED led_216 (.in(and_92_out));
  LED led_217 (.in(and_93_out));
  assign IR2RAMA = and_84_out ? and_84_out : 1'bz;  // Driver driver_145
  assign RAMD2IND = and_84_out ? and_84_out : 1'bz;  // Driver driver_146
  assign RAM_OE = and_84_out ? and_84_out : 1'bz;  // Driver driver_147
  assign IND_CK = and_94_out ? and_94_out : 1'bz;  // Driver driver_148
  assign IND2RAMA = and_85_out ? and_85_out : 1'bz;  // Driver driver_149
  assign RAM_OE = and_85_out ? and_85_out : 1'bz;  // Driver driver_150
  assign IND2RAMA = and_86_out ? and_86_out : 1'bz;  // Driver driver_151
  assign RAM_OE = and_86_out ? and_86_out : 1'bz;  // Driver driver_152
  assign DATA_CK = and_86_out ? and_86_out : 1'bz;  // Driver driver_153
  assign LD2INC = and_86_out ? and_86_out : 1'bz;  // Driver driver_154
  assign IND2RAMA = and_87_out ? and_87_out : 1'bz;  // Driver driver_155
  assign RAM_WE = and_87_out ? and_87_out : 1'bz;  // Driver driver_156
  assign INC2RAMD = and_87_out ? and_87_out : 1'bz;  // Driver driver_157
  assign LD2INC = and_87_out ? and_87_out : 1'bz;  // Driver driver_158
  assign IND2RAMA = and_88_out ? and_88_out : 1'bz;  // Driver driver_159
  assign RAM_OE = and_88_out ? and_88_out : 1'bz;  // Driver driver_160
  assign LD2INC = and_88_out ? and_88_out : 1'bz;  // Driver driver_161
  assign PC_CK = and_89_out ? and_89_out : 1'bz;  // Driver driver_162
  assign LD2INC = and_89_out ? and_89_out : 1'bz;  // Driver driver_163
  assign IR2RAMA = CNT_ISZ_IA ? CNT_ISZ_IA : 1'bz;  // Driver driver_164
  assign RAM_OE = CNT_ISZ_IA ? CNT_ISZ_IA : 1'bz;  // Driver driver_165
  assign IND2INC = CNT_ISZ_IA ? CNT_ISZ_IA : 1'bz;  // Driver driver_166
  assign IND_CK = and_91_out ? and_91_out : 1'bz;  // Driver driver_167
  assign INC2RAMD = and_92_out ? and_92_out : 1'bz;  // Driver driver_168
  assign IND2INC = and_92_out ? and_92_out : 1'bz;  // Driver driver_169
  assign IR2RAMA = and_92_out ? and_92_out : 1'bz;  // Driver driver_170
  assign RAM_WE = and_93_out ? and_93_out : 1'bz;  // Driver driver_171
  and and_95 (CNT_DCA, DCA, NOIND, CK1);
  LED led_218 (.in(CNT_DCA));
  and and_96 (and_96_out, DCA, NOIND, STB1);
  LED led_219 (.in(and_96_out));
  and and_97 (and_97_out, DCA, NOIND, CK2);
  LED led_220 (.in(and_97_out));
  assign IR2RAMA = CNT_DCA ? CNT_DCA : 1'bz;  // Driver driver_172
  assign AC2RAMD = CNT_DCA ? CNT_DCA : 1'bz;  // Driver driver_173
  assign RAM_WE = and_96_out ? and_96_out : 1'bz;  // Driver driver_174
  assign CLA = and_96_out ? and_96_out : 1'bz;  // Driver driver_175
  assign CLAx = and_97_out ? and_97_out : 1'bz;  // Driver driver_176
  assign ROT2AC = and_97_out ? and_97_out : 1'bz;  // Driver driver_177
  assign AC_CK = and_97_out ? and_97_out : 1'bz;  // Driver driver_178
  and and_98 (CNT_DCA_I, DCA, IND, CK1);
  and and_99 (and_99_out, DCA, IND, STB1);
  and and_100 (and_100_out, DCA, IND, CK2);
  and and_101 (and_101_out, DCA, IND, STB2);
  and and_102 (and_102_out, DCA, IND, CK3);
  LED led_221 (.in(CNT_DCA_I));
  LED led_222 (.in(and_99_out));
  LED led_223 (.in(and_100_out));
  LED led_224 (.in(and_101_out));
  LED led_225 (.in(and_102_out));
  assign IR2RAMA = CNT_DCA_I ? CNT_DCA_I : 1'bz;  // Driver driver_179
  assign RAMD2IND = CNT_DCA_I ? CNT_DCA_I : 1'bz;  // Driver driver_180
  assign RAM_OE = CNT_DCA_I ? CNT_DCA_I : 1'bz;  // Driver driver_181
  assign IR2RAMA = and_99_out ? and_99_out : 1'bz;  // Driver driver_182
  assign RAMD2IND = and_99_out ? and_99_out : 1'bz;  // Driver driver_183
  assign RAM_OE = and_99_out ? and_99_out : 1'bz;  // Driver driver_184
  assign IND_CK = and_99_out ? and_99_out : 1'bz;  // Driver driver_185
  assign IND2RAMA = and_100_out ? and_100_out : 1'bz;  // Driver driver_186
  assign AC2RAMD = and_100_out ? and_100_out : 1'bz;  // Driver driver_187
  assign RAM_WE = and_101_out ? and_101_out : 1'bz;  // Driver driver_188
  assign CLA = and_101_out ? and_101_out : 1'bz;  // Driver driver_189
  assign CLAx = and_102_out ? and_102_out : 1'bz;  // Driver driver_190
  assign ROT2AC = and_102_out ? and_102_out : 1'bz;  // Driver driver_191
  assign AC_CK = and_102_out ? and_102_out : 1'bz;  // Driver driver_192
  and and_103 (CNT_DCA_IA, DCA, AUTOIND, CK1);
  and and_104 (and_104_out, DCA, AUTOIND, STB1);
  and and_105 (and_105_out, DCA, AUTOIND, CK2);
  and and_106 (and_106_out, DCA, AUTOIND, STB2);
  and and_107 (and_107_out, DCA, AUTOIND, CK3);
  and and_108 (and_108_out, DCA, AUTOIND, STB3);
  and and_109 (and_109_out, DCA, AUTOIND, CK4);
  LED led_226 (.in(and_109_out));
  and and_110 (and_110_out, DCA, AUTOIND, STB4);
  LED led_227 (.in(and_110_out));
  and and_111 (and_111_out, DCA, AUTOIND, CK5);
  LED led_228 (.in(and_111_out));
  LED led_229 (.in(CNT_DCA_IA));
  LED led_230 (.in(and_104_out));
  LED led_231 (.in(and_105_out));
  LED led_232 (.in(and_106_out));
  assign IR2RAMA = and_107_out ? and_107_out : 1'bz;  // Driver driver_193
  LED led_233 (.in(and_107_out));
  assign RAMD2IND = and_107_out ? and_107_out : 1'bz;  // Driver driver_194
  assign RAM_OE = and_107_out ? and_107_out : 1'bz;  // Driver driver_195
  LED led_234 (.in(and_108_out));
  assign IND_CK = and_108_out ? and_108_out : 1'bz;  // Driver driver_196
  assign IND2RAMA = and_109_out ? and_109_out : 1'bz;  // Driver driver_197
  assign AC2RAMD = and_109_out ? and_109_out : 1'bz;  // Driver driver_198
  Driver driver_199 (.in(and_109_out), .en(and_109_out));  // open: out
  Driver driver_200 (.in(and_109_out), .en(and_109_out));  // open: out
  Driver driver_201 (.in(and_109_out), .en(and_109_out));  // open: out
  Driver driver_202 (.in(and_110_out), .en(and_110_out));  // open: out
  Driver driver_203 (.in(and_110_out), .en(and_110_out));  // open: out
  assign RAM_WE = and_110_out ? and_110_out : 1'bz;  // Driver driver_204
  assign CLA = and_110_out ? and_110_out : 1'bz;  // Driver driver_205
  Driver driver_206 (.in(and_110_out), .en(and_110_out));  // open: out
  assign CLAx = and_111_out ? and_111_out : 1'bz;  // Driver driver_207
  assign ROT2AC = and_111_out ? and_111_out : 1'bz;  // Driver driver_208
  assign AC_CK = and_111_out ? and_111_out : 1'bz;  // Driver driver_209
  Driver driver_210 (.in(and_111_out), .en(and_111_out));  // open: out
  Driver driver_211 (.in(and_111_out), .en(and_111_out));  // open: out
  assign IR2RAMA = CNT_DCA_IA ? CNT_DCA_IA : 1'bz;  // Driver driver_212
  assign RAM_OE = CNT_DCA_IA ? CNT_DCA_IA : 1'bz;  // Driver driver_213
  assign IND2INC = CNT_DCA_IA ? CNT_DCA_IA : 1'bz;  // Driver driver_214
  assign IND_CK = and_104_out ? and_104_out : 1'bz;  // Driver driver_215
  assign INC2RAMD = and_105_out ? and_105_out : 1'bz;  // Driver driver_216
  assign IND2INC = and_105_out ? and_105_out : 1'bz;  // Driver driver_217
  assign IR2RAMA = and_105_out ? and_105_out : 1'bz;  // Driver driver_218
  assign RAM_WE = and_106_out ? and_106_out : 1'bz;  // Driver driver_219
  and and_112 (CNT_JMS, JMS, NOIND, CK1);
  and and_113 (and_113_out, JMS, NOIND, STB1);
  and and_114 (and_114_out, JMS, NOIND, CK2);
  and and_115 (and_115_out, JMS, NOIND, STB2);
  and and_116 (and_116_out, JMS, NOIND, STB3);
  LED led_235 (.in(CNT_JMS));
  Driver driver_220 (.in(and_113_out), .en(and_113_out));  // open: out
  LED led_236 (.in(and_113_out));
  Driver driver_221 (.in(and_113_out), .en(and_113_out));  // open: out
  assign RAM_WE = and_113_out ? and_113_out : 1'bz;  // Driver driver_222
  assign IR2PC = and_113_out ? and_113_out : 1'bz;  // Driver driver_223
  assign driver_224_out = and_113_out ? and_113_out : 1'bz;  // Driver driver_224
  LED led_237 (.in(and_114_out));
  LED led_238 (.in(and_115_out));
  LED led_239 (.in(and_116_out));
  assign PC2RAMD = CNT_JMS ? CNT_JMS : 1'bz;  // Driver driver_225
  assign IR2RAMA = CNT_JMS ? CNT_JMS : 1'bz;  // Driver driver_226
  assign driver_227_out = CNT_JMS ? CNT_JMS : 1'bz;  // Driver driver_227
  assign driver_228_out = CNT_JMS ? CNT_JMS : 1'bz;  // Driver driver_228
  assign driver_229_out = CNT_JMS ? CNT_JMS : 1'bz;  // Driver driver_229
  assign IR2PC = and_114_out ? and_114_out : 1'bz;  // Driver driver_230
  assign PC_LD = and_114_out ? and_114_out : 1'bz;  // Driver driver_231
  Driver driver_232 (.in(and_114_out), .en(and_114_out));  // open: out
  assign driver_233_out = and_114_out ? and_114_out : 1'bz;  // Driver driver_233
  assign driver_234_out = and_114_out ? and_114_out : 1'bz;  // Driver driver_234
  Driver driver_235 (.in(and_115_out), .en(and_115_out));  // open: out
  Driver driver_236 (.in(and_115_out), .en(and_115_out));  // open: out
  assign PC_CK = and_115_out ? and_115_out : 1'bz;  // Driver driver_237
  assign driver_238_out = and_115_out ? and_115_out : 1'bz;  // Driver driver_238
  assign driver_239_out = and_115_out ? and_115_out : 1'bz;  // Driver driver_239
  assign PC_CK = and_116_out ? and_116_out : 1'bz;  // Driver driver_240
  and and_117 (and_117_out, JMS, IND, CK2);
  and and_118 (and_118_out, JMS, IND, CK3);
  and and_119 (and_119_out, JMS, IND, CK4);
  and and_120 (and_120_out, JMS, IND, CK5);
  and and_121 (and_121_out, JMS, IND, CK6);
  and and_122 (CNT_JMS_I, JMS, IND, CK1);
  and and_123 (and_123_out, JMS, IND, STB1);
  LED led_240 (.in(and_117_out));
  LED led_241 (.in(and_118_out));
  LED led_242 (.in(and_119_out));
  LED led_243 (.in(and_120_out));
  LED led_244 (.in(and_121_out));
  LED led_245 (.in(CNT_JMS_I));
  LED led_246 (.in(and_123_out));
  assign IND2RAMA = and_117_out ? and_117_out : 1'bz;  // Driver driver_241
  assign PC2RAMD = and_117_out ? and_117_out : 1'bz;  // Driver driver_242
  assign IND2RAMA = and_118_out ? and_118_out : 1'bz;  // Driver driver_243
  assign PC2RAMD = and_118_out ? and_118_out : 1'bz;  // Driver driver_244
  assign RAM_WE = and_118_out ? and_118_out : 1'bz;  // Driver driver_245
  assign PC_LD = and_118_out ? and_118_out : 1'bz;  // Driver driver_246
  assign IND2PC = and_118_out ? and_118_out : 1'bz;  // Driver driver_247
  assign IND2PC = and_119_out ? and_119_out : 1'bz;  // Driver driver_248
  assign PC_LD = and_119_out ? and_119_out : 1'bz;  // Driver driver_249
  assign PC_CK = and_119_out ? and_119_out : 1'bz;  // Driver driver_250
  assign IND2PC = and_120_out ? and_120_out : 1'bz;  // Driver driver_251
  assign PC_LD = and_120_out ? and_120_out : 1'bz;  // Driver driver_252
  assign PC_CK = and_121_out ? and_121_out : 1'bz;  // Driver driver_253
  assign IR2RAMA = CNT_JMS_I ? CNT_JMS_I : 1'bz;  // Driver driver_254
  assign RAMD2IND = CNT_JMS_I ? CNT_JMS_I : 1'bz;  // Driver driver_255
  assign RAM_OE = CNT_JMS_I ? CNT_JMS_I : 1'bz;  // Driver driver_256
  assign IND_CK = and_123_out ? and_123_out : 1'bz;  // Driver driver_257
  and and_124 (CNT_JMS_IA, JMS, AUTOIND, CK1);
  and and_125 (and_125_out, JMS, AUTOIND, STB1);
  and and_126 (and_126_out, JMS, AUTOIND, CK2);
  and and_127 (and_127_out, JMS, AUTOIND, STB2);
  and and_128 (and_128_out, JMS, AUTOIND, CK3);
  and and_129 (and_129_out, JMS, AUTOIND, STB3);
  and and_130 (and_130_out, JMS, AUTOIND, CK4);
  and and_131 (and_131_out, JMS, AUTOIND, CK5);
  and and_132 (and_132_out, JMS, AUTOIND, CK6);
  and and_133 (and_133_out, JMS, AUTOIND, CK7);
  and and_134 (and_134_out, JMS, AUTOIND, CK8);
  assign IR2RAMA = CNT_JMS_IA ? CNT_JMS_IA : 1'bz;  // Driver driver_258
  LED led_247 (.in(CNT_JMS_IA));
  assign RAM_OE = CNT_JMS_IA ? CNT_JMS_IA : 1'bz;  // Driver driver_259
  assign IND2INC = CNT_JMS_IA ? CNT_JMS_IA : 1'bz;  // Driver driver_260
  LED led_248 (.in(and_125_out));
  assign IND_CK = and_125_out ? and_125_out : 1'bz;  // Driver driver_261
  assign INC2RAMD = and_126_out ? and_126_out : 1'bz;  // Driver driver_262
  LED led_249 (.in(and_126_out));
  assign IND2INC = and_126_out ? and_126_out : 1'bz;  // Driver driver_263
  assign IR2RAMA = and_126_out ? and_126_out : 1'bz;  // Driver driver_264
  LED led_250 (.in(and_127_out));
  assign RAM_WE = and_127_out ? and_127_out : 1'bz;  // Driver driver_265
  assign IR2RAMA = and_128_out ? and_128_out : 1'bz;  // Driver driver_266
  LED led_251 (.in(and_128_out));
  assign RAMD2IND = and_128_out ? and_128_out : 1'bz;  // Driver driver_267
  assign RAM_OE = and_128_out ? and_128_out : 1'bz;  // Driver driver_268
  LED led_252 (.in(and_129_out));
  assign IND_CK = and_129_out ? and_129_out : 1'bz;  // Driver driver_269
  assign IND2RAMA = and_130_out ? and_130_out : 1'bz;  // Driver driver_270
  LED led_253 (.in(and_130_out));
  assign PC2RAMD = and_130_out ? and_130_out : 1'bz;  // Driver driver_271
  assign IND2RAMA = and_131_out ? and_131_out : 1'bz;  // Driver driver_272
  LED led_254 (.in(and_131_out));
  assign PC2RAMD = and_131_out ? and_131_out : 1'bz;  // Driver driver_273
  assign RAM_WE = and_131_out ? and_131_out : 1'bz;  // Driver driver_274
  assign PC_LD = and_131_out ? and_131_out : 1'bz;  // Driver driver_275
  assign IND2PC = and_131_out ? and_131_out : 1'bz;  // Driver driver_276
  assign IND2PC = and_132_out ? and_132_out : 1'bz;  // Driver driver_277
  LED led_255 (.in(and_132_out));
  assign PC_LD = and_132_out ? and_132_out : 1'bz;  // Driver driver_278
  assign PC_CK = and_132_out ? and_132_out : 1'bz;  // Driver driver_279
  assign IND2PC = and_133_out ? and_133_out : 1'bz;  // Driver driver_280
  LED led_256 (.in(and_133_out));
  assign PC_LD = and_133_out ? and_133_out : 1'bz;  // Driver driver_281
  LED led_257 (.in(and_134_out));
  assign PC_CK = and_134_out ? and_134_out : 1'bz;  // Driver driver_282
  and and_135 (CNT_JMP, JMP, NOIND, CK1);
  and and_136 (and_136_out, JMP, NOIND, STB1);
  LED led_258 (.in(CNT_JMP));
  LED led_259 (.in(and_136_out));
  assign IR2PC = CNT_JMP ? CNT_JMP : 1'bz;  // Driver driver_283
  assign PC_LD = CNT_JMP ? CNT_JMP : 1'bz;  // Driver driver_284
  assign PC_CK = and_136_out ? and_136_out : 1'bz;  // Driver driver_285
  and and_137 (CNT_JMP_I, JMP, IND, CK1);
  and and_138 (and_138_out, JMP, IND, STB1);
  LED led_260 (.in(CNT_JMP_I));
  LED led_261 (.in(and_138_out));
  assign IR2RAMA = CNT_JMP_I ? CNT_JMP_I : 1'bz;  // Driver driver_286
  assign RAMD2PC = CNT_JMP_I ? CNT_JMP_I : 1'bz;  // Driver driver_287
  assign RAM_OE = CNT_JMP_I ? CNT_JMP_I : 1'bz;  // Driver driver_288
  assign PC_LD = CNT_JMP_I ? CNT_JMP_I : 1'bz;  // Driver driver_289
  assign PC_CK = and_138_out ? and_138_out : 1'bz;  // Driver driver_290
  and and_139 (CNT_JMP_IA, JMP, AUTOIND, CK1);
  and and_140 (and_140_out, JMP, AUTOIND, STB1);
  and and_141 (and_141_out, JMP, AUTOIND, CK2);
  and and_142 (and_142_out, JMP, AUTOIND, STB2);
  and and_143 (and_143_out, JMP, AUTOIND, CK3);
  and and_144 (and_144_out, JMP, AUTOIND, STB3);
  LED led_262 (.in(CNT_JMP_IA));
  LED led_263 (.in(and_140_out));
  LED led_264 (.in(and_141_out));
  LED led_265 (.in(and_142_out));
  LED led_266 (.in(and_143_out));
  LED led_267 (.in(and_144_out));
  assign IR2RAMA = CNT_JMP_IA ? CNT_JMP_IA : 1'bz;  // Driver driver_291
  assign RAM_OE = CNT_JMP_IA ? CNT_JMP_IA : 1'bz;  // Driver driver_292
  assign IND2INC = CNT_JMP_IA ? CNT_JMP_IA : 1'bz;  // Driver driver_293
  assign IND_CK = and_140_out ? and_140_out : 1'bz;  // Driver driver_294
  assign INC2RAMD = and_141_out ? and_141_out : 1'bz;  // Driver driver_295
  assign IND2INC = and_141_out ? and_141_out : 1'bz;  // Driver driver_296
  assign IR2RAMA = and_141_out ? and_141_out : 1'bz;  // Driver driver_297
  assign RAM_WE = and_142_out ? and_142_out : 1'bz;  // Driver driver_298
  assign IR2RAMA = and_143_out ? and_143_out : 1'bz;  // Driver driver_299
  assign RAMD2PC = and_143_out ? and_143_out : 1'bz;  // Driver driver_300
  assign RAM_OE = and_143_out ? and_143_out : 1'bz;  // Driver driver_301
  assign PC_LD = and_143_out ? and_143_out : 1'bz;  // Driver driver_302
  assign PC_CK = and_144_out ? and_144_out : 1'bz;  // Driver driver_303
  and and_145 (CNT_OPR1, OPR1, CK1);
  and and_146 (and_146_out, OPR1, STB1);
  LED led_268 (.in(CNT_OPR1));
  LED led_269 (.in(and_146_out));
  assign ROT2AC = CNT_OPR1 ? CNT_OPR1 : 1'bz;  // Driver driver_304
  assign LINK_CK = and_146_out ? and_146_out : 1'bz;  // Driver driver_305
  assign AC_CK = and_146_out ? and_146_out : 1'bz;  // Driver driver_306
  and and_147 (CNT_OPR2, OPR2, CK1);
  and and_148 (and_148_out, OPR2, SKIP, STB1);
  and and_149 (and_149_out, OPR2, CK2);
  and and_150 (and_150_out, OPR2, STB2);
  LED led_270 (.in(CNT_OPR2));
  assign ROT2AC = CNT_OPR2 ? CNT_OPR2 : 1'bz;  // Driver driver_307
  LED led_271 (.in(and_148_out));
  assign PC_CK = and_148_out ? and_148_out : 1'bz;  // Driver driver_308
  assign ROT2AC = and_149_out ? and_149_out : 1'bz;  // Driver driver_309
  LED led_272 (.in(and_149_out));
  assign MQ_CK = and_149_out ? and_149_out : 1'bz;  // Driver driver_310
  LED led_273 (.in(and_150_out));
  assign AC_CK = and_150_out ? and_150_out : 1'bz;  // Driver driver_311
  not not_4 (not_4_out, OPR_SWP);
  not not_5 (not_5_out, OPR_SWP);
  and and_151 (CNT_OPR3, OPR3, 1'b1, CK1);
  and and_152 (and_152_out, OPR3, not_4_out, STB1);
  and and_153 (and_153_out, OPR3, CK2);
  and and_154 (and_154_out, OPR3, not_5_out, STB2);
  LED led_274 (.in(CNT_OPR3));
  LED led_275 (.in(and_152_out));
  LED led_276 (.in(and_153_out));
  LED led_277 (.in(and_154_out));
  assign ROT2AC = CNT_OPR3 ? CNT_OPR3 : 1'bz;  // Driver driver_312
  assign MQ_CK = and_152_out ? and_152_out : 1'bz;  // Driver driver_313
  assign ROT2AC = and_153_out ? and_153_out : 1'bz;  // Driver driver_314
  assign AC_CK = and_154_out ? and_154_out : 1'bz;  // Driver driver_315
  or or_19 (or_19_out, CK1, CK2, CK3, CK4, CK5, CK6, CK7, CK8, CK9);
  LED led_278 (.in(IOT));
  Demultiplexer #(.Selector_Bits(3)) demultiplexer_1 (
    .sel(BUS_IR[2:0]), .in(IOT_DEVPRI), .out_0(IOT_TFL), .out_1(IOT_TSF), .out_2(IOT_TCF),
    .out_3(demultiplexer_1_out_3), .out_4(IOT_TPC), .out_5(IOT_TSK), .out_6(IOT_TLS),
    .out_7(demultiplexer_1_out_7));
  LED led_279 (.in(IOT_DEVPRI));
  Demultiplexer #(.Selector_Bits(3)) demultiplexer_2 (
    .sel(BUS_IR[2:0]), .in(IOT_DEVKBD), .out_0(IOT_KCF), .out_1(IOT_KSF), .out_2(IOT_KCC),
    .out_3(demultiplexer_2_out_3), .out_4(IOT_KRS), .out_5(IOT_KIE), .out_6(IOT_KRB),
    .out_7(demultiplexer_2_out_7));
  LED led_280 (.in(IOT_DEVKBD));
  Demultiplexer #(.Selector_Bits(3)) demultiplexer_3 (
    .sel(BUS_IR[2:0]), .in(IOT_DEVCPU), .out_0(IOT_SKON), .out_1(IOT_ION), .out_2(IOT_IOF), .out_3(IOT_SRQ),
    .out_4(IOT_GTF), .out_5(IOT_RTF), .out_6(IOT_SGT), .out_7(IOT_CAF));
  LED led_281 (.in(IOT_DEVCPU));
  // Probe on BUS_IR[2:0]
  // Probe on BUS_IR[8:3]
  and and_155 (and_155_out, or_19_out, IOT);
  Demultiplexer #(.Selector_Bits(6)) demultiplexer_4 (
    .sel(BUS_IR[8:3]), .in(and_155_out), .out_0(IOT_DEVCPU), .out_1(IOT_DEVHSR), .out_2(IOT_DEVHSP),
    .out_3(IOT_DEVKBD), .out_4(IOT_DEVPRI), .out_5(IOT_DEV5), .out_6(IOT_DEV6), .out_7(IOT_DEV7),
    .out_8(IOT_DEV8), .out_9(IOT_DEV9), .out_10(demultiplexer_4_out_10), .out_11(demultiplexer_4_out_11),
    .out_12(demultiplexer_4_out_12), .out_13(demultiplexer_4_out_13), .out_14(demultiplexer_4_out_14),
    .out_15(demultiplexer_4_out_15), .out_16(demultiplexer_4_out_16), .out_17(demultiplexer_4_out_17),
    .out_18(demultiplexer_4_out_18), .out_19(demultiplexer_4_out_19), .out_20(demultiplexer_4_out_20),
    .out_21(demultiplexer_4_out_21), .out_22(demultiplexer_4_out_22), .out_23(demultiplexer_4_out_23),
    .out_24(demultiplexer_4_out_24), .out_25(demultiplexer_4_out_25), .out_26(demultiplexer_4_out_26),
    .out_27(demultiplexer_4_out_27), .out_28(demultiplexer_4_out_28), .out_29(demultiplexer_4_out_29),
    .out_30(demultiplexer_4_out_30), .out_31(demultiplexer_4_out_31), .out_32(demultiplexer_4_out_32),
    .out_33(demultiplexer_4_out_33), .out_34(demultiplexer_4_out_34), .out_35(demultiplexer_4_out_35),
    .out_36(demultiplexer_4_out_36), .out_37(demultiplexer_4_out_37), .out_38(demultiplexer_4_out_38),
    .out_39(demultiplexer_4_out_39), .out_40(demultiplexer_4_out_40), .out_41(demultiplexer_4_out_41),
    .out_42(demultiplexer_4_out_42), .out_43(demultiplexer_4_out_43), .out_44(demultiplexer_4_out_44),
    .out_45(demultiplexer_4_out_45), .out_46(demultiplexer_4_out_46), .out_47(demultiplexer_4_out_47),
    .out_48(demultiplexer_4_out_48), .out_49(demultiplexer_4_out_49), .out_50(demultiplexer_4_out_50),
    .out_51(demultiplexer_4_out_51), .out_52(demultiplexer_4_out_52), .out_53(demultiplexer_4_out_53),
    .out_54(demultiplexer_4_out_54), .out_55(demultiplexer_4_out_55), .out_56(demultiplexer_4_out_56),
    .out_57(demultiplexer_4_out_57), .out_58(demultiplexer_4_out_58), .out_59(demultiplexer_4_out_59),
    .out_60(demultiplexer_4_out_60), .out_61(demultiplexer_4_out_61), .out_62(demultiplexer_4_out_62),
    .out_63(demultiplexer_4_out_63));
  or or_20 (IOT_DEV5x, demultiplexer_4_out_50, demultiplexer_4_out_51, demultiplexer_4_out_52, demultiplexer_4_out_53, demultiplexer_4_out_54, demultiplexer_4_out_56, demultiplexer_4_out_57, demultiplexer_4_out_58, demultiplexer_4_out_59, demultiplexer_4_out_55);
  or or_21 (IOT_DEV6x, demultiplexer_4_out_60, demultiplexer_4_out_61, demultiplexer_4_out_63, demultiplexer_4_out_62);
  and and_156 (and_156_out, OPR3, OPR_SWP, STB1);
  or or_22 (IOT_DEV3x, demultiplexer_4_out_30, demultiplexer_4_out_31, demultiplexer_4_out_32, demultiplexer_4_out_33, demultiplexer_4_out_34, demultiplexer_4_out_36, demultiplexer_4_out_37, demultiplexer_4_out_38, demultiplexer_4_out_39, demultiplexer_4_out_35);
  or or_23 (IOT_DEV4x, demultiplexer_4_out_40, demultiplexer_4_out_41, demultiplexer_4_out_42, demultiplexer_4_out_43, demultiplexer_4_out_44, demultiplexer_4_out_46, demultiplexer_4_out_47, demultiplexer_4_out_48, demultiplexer_4_out_49, demultiplexer_4_out_45);
  LED led_282 (.in(and_156_out));
  Seven_Seg_Hex seven_seg_hex_42 (.d(CK_NUM), .dp(1'b0));
  or or_24 (IOT_DEV1x, demultiplexer_4_out_10, demultiplexer_4_out_11, demultiplexer_4_out_12, demultiplexer_4_out_13, demultiplexer_4_out_14, demultiplexer_4_out_16, demultiplexer_4_out_17, demultiplexer_4_out_18, demultiplexer_4_out_19, demultiplexer_4_out_15);
  or or_25 (IOT_DEV2x, demultiplexer_4_out_20, demultiplexer_4_out_21, demultiplexer_4_out_22, demultiplexer_4_out_23, demultiplexer_4_out_24, demultiplexer_4_out_26, demultiplexer_4_out_27, demultiplexer_4_out_28, demultiplexer_4_out_29, demultiplexer_4_out_25);
  assign MQ_CK = and_156_out ? and_156_out : 1'bz;  // Driver driver_316
  assign AC_CK = and_156_out ? and_156_out : 1'bz;  // Driver driver_317
  Driver driver_318 (.in(and_156_out), .en(and_156_out));  // open: out
  Driver driver_319 (.in(and_156_out), .en(and_156_out));  // open: out
  Driver driver_320 (.in(and_156_out), .en(and_156_out));  // open: out
  // Probe on LATCHED_PC
  LED led_283 (.in(PH_FIRST));
  LED led_284 (.in(PH_STB));
  LED led_285 (.in(PH_LAST));
  // Probe on BUS_IR
  Demultiplexer #(.Selector_Bits(3)) demultiplexer_5 (
    .sel(BUS_IR[11:9]), .in(1'b1), .out_0(AND), .out_1(TAD), .out_2(ISZ), .out_3(DCA), .out_4(JMS),
    .out_5(JMP), .out_6(IOT), .out_7(OPR));
  LED led_286 (.in(OPR));
  Demultiplexer #(.Selector_Bits(2)) demultiplexer_6 (
    .sel({BUS_IR[8], BUS_IR[0]}), .in(OPR), .out_0(demultiplexer_6_out_0), .out_1(demultiplexer_6_out_1),
    .out_2(OPR2), .out_3(OPR3));
  and and_157 (and_157_out, BUS_IR[3], ~BUS_IR[4], ~BUS_IR[5], ~BUS_IR[6], ~BUS_IR[7], BUS_IR[8]);  // And
  LED led_287 (.in(and_157_out));
  not not_6 (not_6_out, BUS_IR[8]);
  or or_26 (OPR1, demultiplexer_6_out_0, demultiplexer_6_out_1);
  nor nor_2 (nor_2_out, and_157_out, not_6_out);
  LED led_288 (.in(OPR1));
  LED led_289 (.in(nor_2_out));
  nor nor_3 (nor_3_out, OPR, IOT);
  nor nor_4 (nor_4_out, BUS_IR[0], BUS_IR[1], BUS_IR[2], BUS_IR[3], BUS_IR[4], BUS_IR[5], BUS_IR[6], BUS_IR[7]);
  and and_158 (AUTOIND, nor_3_out, and_157_out);
  and and_159 (IND, nor_3_out, nor_2_out);
  and and_160 (NOIND, nor_3_out, not_6_out);
  and and_161 (MP, nor_3_out, BUS_IR[7]);
  and and_162 (OPR_IAC, BUS_IR[0], OPR1);
  LED led_290 (.in(OPR_IAC));
  and and_163 (OPR_X2, BUS_IR[1], OPR1);
  LED led_291 (.in(OPR_X2));
  and and_164 (OPR_LEFT, BUS_IR[2], OPR1);
  LED led_292 (.in(OPR_LEFT));
  and and_165 (OPR_RIGHT, BUS_IR[3], OPR1);
  LED led_293 (.in(OPR_RIGHT));
  and and_166 (OPR_CML, BUS_IR[4], OPR1);
  LED led_294 (.in(OPR_CML));
  and and_167 (OPR_CMA, BUS_IR[5], OPR1);
  LED led_295 (.in(OPR_CMA));
  and and_168 (OPR_CLL, BUS_IR[6], OPR1);
  LED led_296 (.in(OPR_CLL));
  and and_169 (OPR_CLA1, BUS_IR[7], OPR1);
  LED led_297 (.in(OPR_CLA1));
  and and_170 (OPR_NA1, BUS_IR[0], OPR2);
  LED led_298 (.in(OPR_NA1));
  and and_171 (OPR_HLT, BUS_IR[1], OPR2);
  LED led_299 (.in(OPR_HLT));
  and and_172 (OPR_OSR, BUS_IR[2], OPR2);
  LED led_300 (.in(OPR_OSR));
  and and_173 (OPR_TSTINV, BUS_IR[3], OPR2);
  LED led_301 (.in(OPR_TSTINV));
  and and_174 (OPR_SNLSZL, BUS_IR[4], OPR2);
  LED led_302 (.in(OPR_SNLSZL));
  and and_175 (OPR_SZASNA, BUS_IR[5], OPR2);
  LED led_303 (.in(OPR_SZASNA));
  and and_176 (OPR_SMASPA, BUS_IR[6], OPR2);
  LED led_304 (.in(OPR_SMASPA));
  and and_177 (OPR_CLA2, BUS_IR[7], OPR2);
  LED led_305 (.in(OPR_CLA2));
  and and_178 (and_178_out, OPR3, BUS_IR[0]);
  and and_179 (and_179_out[0], OPR3, BUS_IR[1]);
  and and_180 (and_179_out[1], OPR3, BUS_IR[2]);
  and and_181 (and_179_out[2], OPR3, BUS_IR[3]);
  and and_182 (and_182_out, OPR3, BUS_IR[4]);
  and and_183 (OPR_SCA, OPR3, BUS_IR[5]);
  and and_184 (and_184_out, OPR3, BUS_IR[6]);
  and and_185 (OPR_CLA3, OPR3, BUS_IR[7]);
  LED led_306 (.in(AUTOIND));
  LED led_307 (.in(IND));
  LED led_308 (.in(NOIND));
  LED led_309 (.in(MP));
  LED led_310 (.in(OPR3));
  LED led_311 (.in(and_178_out));
  LED led_312 (.in(and_179_out[0]));
  LED led_313 (.in(and_179_out[1]));
  LED led_314 (.in(and_179_out[2]));
  LED led_315 (.in(and_182_out));
  LED led_316 (.in(OPR_SCA));
  LED led_317 (.in(and_184_out));
  LED led_318 (.in(OPR_CLA3));
  and and_186 (OPR_NOP, nor_4_out, OPR);
  LED led_319 (.in(OPR1));
  LED led_320 (.in(OPR2));
  nand nand_1 (nand_1_out, and_182_out, and_184_out);
  LED led_321 (.in(OPR_NOP));
  LED led_322 (.in(nand_1_out));
  Seven_Seg_Hex seven_seg_hex_43 (.d(CK_NUM), .dp(1'b0));
  and and_187 (OPR_MQL, and_182_out, and_182_out);
  not not_7 (OPR_SWP, nand_1_out);
  and and_188 (OPR_MQA, and_184_out, and_184_out);
  // Probe on LATCHED_PC
  LED led_323 (.in(PH_FIRST));
  LED led_324 (.in(OPR_MQL));
  LED led_325 (.in(OPR_MQA));
  LED led_326 (.in(PH_STB));
  LED led_327 (.in(PH_LAST));
  Decoder #(.Selector_Bits(3)) decoder_1 (
    .sel(and_179_out), .out_0(OPR_OPERATION), .out_1(OPR_SCL), .out_2(OPR_MUY), .out_3(OPR_DVI),
    .out_4(OPR_NMI), .out_5(OPR_SHL), .out_6(OPR_ASL), .out_7(OPR_LSR));
  LED led_328 (.in(OPR_OPERATION));
  LED led_329 (.in(OPR_SCL));
  LED led_330 (.in(OPR_MUY));
  LED led_331 (.in(OPR_DVI));
  LED led_332 (.in(OPR_NMI));
  LED led_333 (.in(OPR_SHL));
  LED led_334 (.in(OPR_ASL));
  LED led_335 (.in(OPR_LSR));
  Demultiplexer #(.Selector_Bits(3)) demultiplexer_7 (
    .sel(BUS_IR[2:0]), .in(L_DEVPRI), .out_0(L_TFL), .out_1(L_TSF), .out_2(L_TCF),
    .out_3(demultiplexer_7_out_3), .out_4(L_TPC), .out_5(L_TSK), .out_6(L_TLS), .out_7(demultiplexer_7_out_7));
  LED led_336 (.in(L_DEVPRI));
  Demultiplexer #(.Selector_Bits(3)) demultiplexer_8 (
    .sel(BUS_IR[2:0]), .in(L_DEVKBD), .out_0(L_KCF), .out_1(L_KSF), .out_2(L_KCC),
    .out_3(demultiplexer_8_out_3), .out_4(L_KRS), .out_5(L_KIE), .out_6(L_KRB), .out_7(demultiplexer_8_out_7));
  LED led_337 (.in(L_DEVKBD));
  Demultiplexer #(.Selector_Bits(3)) demultiplexer_9 (
    .sel(BUS_IR[2:0]), .in(L_DEVCPU), .out_0(L_SKON), .out_1(L_ION), .out_2(L_IOF), .out_3(L_SRQ),
    .out_4(L_GTF), .out_5(L_RTF), .out_6(L_SGT), .out_7(L_CAF));
  LED led_338 (.in(L_DEVCPU));
  // Probe on BUS_IR[2:0]
  // Probe on BUS_IR[8:3]
  LED led_339 (.in(IOT));
  Demultiplexer #(.Selector_Bits(6)) demultiplexer_10 (
    .sel(BUS_IR[8:3]), .in(IOT), .out_0(L_DEVCPU), .out_1(L_DEVHSR), .out_2(L_DEVHSP), .out_3(L_DEVKBD),
    .out_4(L_DEVPRI), .out_5(L_DEV5), .out_6(L_DEV6), .out_7(L_DEV7), .out_8(L_DEV8), .out_9(L_DEV9),
    .out_10(demultiplexer_10_out_10), .out_11(demultiplexer_10_out_11), .out_12(demultiplexer_10_out_12),
    .out_13(demultiplexer_10_out_13), .out_14(demultiplexer_10_out_14), .out_15(demultiplexer_10_out_15),
    .out_16(demultiplexer_10_out_16), .out_17(demultiplexer_10_out_17), .out_18(demultiplexer_10_out_18),
    .out_19(demultiplexer_10_out_19), .out_20(demultiplexer_10_out_20), .out_21(demultiplexer_10_out_21),
    .out_22(demultiplexer_10_out_22), .out_23(demultiplexer_10_out_23), .out_24(demultiplexer_10_out_24),
    .out_25(demultiplexer_10_out_25), .out_26(demultiplexer_10_out_26), .out_27(demultiplexer_10_out_27),
    .out_28(demultiplexer_10_out_28), .out_29(demultiplexer_10_out_29), .out_30(demultiplexer_10_out_30),
    .out_31(demultiplexer_10_out_31), .out_32(demultiplexer_10_out_32), .out_33(demultiplexer_10_out_33),
    .out_34(demultiplexer_10_out_34), .out_35(demultiplexer_10_out_35), .out_36(demultiplexer_10_out_36),
    .out_37(demultiplexer_10_out_37), .out_38(demultiplexer_10_out_38), .out_39(demultiplexer_10_out_39),
    .out_40(demultiplexer_10_out_40), .out_41(demultiplexer_10_out_41), .out_42(demultiplexer_10_out_42),
    .out_43(demultiplexer_10_out_43), .out_44(demultiplexer_10_out_44), .out_45(demultiplexer_10_out_45),
    .out_46(demultiplexer_10_out_46), .out_47(demultiplexer_10_out_47), .out_48(demultiplexer_10_out_48),
    .out_49(demultiplexer_10_out_49), .out_50(demultiplexer_10_out_50), .out_51(demultiplexer_10_out_51),
    .out_52(demultiplexer_10_out_52), .out_53(demultiplexer_10_out_53), .out_54(demultiplexer_10_out_54),
    .out_55(demultiplexer_10_out_55), .out_56(demultiplexer_10_out_56), .out_57(demultiplexer_10_out_57),
    .out_58(demultiplexer_10_out_58), .out_59(demultiplexer_10_out_59), .out_60(demultiplexer_10_out_60),
    .out_61(demultiplexer_10_out_61), .out_62(demultiplexer_10_out_62), .out_63(demultiplexer_10_out_63));
  or or_27 (L_DEV5x, demultiplexer_10_out_50, demultiplexer_10_out_51, demultiplexer_10_out_52, demultiplexer_10_out_53, demultiplexer_10_out_54, demultiplexer_10_out_56, demultiplexer_10_out_57, demultiplexer_10_out_58, demultiplexer_10_out_59, demultiplexer_10_out_55);
  or or_28 (L_DEV6x, demultiplexer_10_out_60, demultiplexer_10_out_61, demultiplexer_10_out_63, demultiplexer_10_out_62);
  or or_29 (L_DEV3x, demultiplexer_10_out_30, demultiplexer_10_out_31, demultiplexer_10_out_32, demultiplexer_10_out_33, demultiplexer_10_out_34, demultiplexer_10_out_36, demultiplexer_10_out_37, demultiplexer_10_out_38, demultiplexer_10_out_39, demultiplexer_10_out_35);
  or or_30 (L_DEV4x, demultiplexer_10_out_40, demultiplexer_10_out_41, demultiplexer_10_out_42, demultiplexer_10_out_43, demultiplexer_10_out_44, demultiplexer_10_out_46, demultiplexer_10_out_47, demultiplexer_10_out_48, demultiplexer_10_out_49, demultiplexer_10_out_45);
  or or_31 (L_DEV1x, demultiplexer_10_out_10, demultiplexer_10_out_11, demultiplexer_10_out_12, demultiplexer_10_out_13, demultiplexer_10_out_14, demultiplexer_10_out_16, demultiplexer_10_out_17, demultiplexer_10_out_18, demultiplexer_10_out_19, demultiplexer_10_out_15);
  or or_32 (L_DEV2x, demultiplexer_10_out_20, demultiplexer_10_out_21, demultiplexer_10_out_22, demultiplexer_10_out_23, demultiplexer_10_out_24, demultiplexer_10_out_26, demultiplexer_10_out_27, demultiplexer_10_out_28, demultiplexer_10_out_29, demultiplexer_10_out_25);
  PullDown pulldown_3 (.out(IR2PC));
  PullDown pulldown_4 (.out(IND2PC));
  PullDown pulldown_5 (.out(RAMD2PC));
  PullDown pulldown_6 (.out(ROT2AC));
  PullDown pulldown_7 (.out(RAMD2AC_ADD));
  PullDown pulldown_8 (.out(PC_LD));
  PullDown pulldown_9 (.out(IND2RAMA));
  PullDown pulldown_10 (.out(INC2RAMD));
  PullDown pulldown_11 (.out(PC2RAMD));
  PullDown pulldown_12 (.out(IR2RAMA));
  PullDown pulldown_13 (.out(IND2INC));
  PullDown pulldown_14 (.out(LD2INC));
  PullDown pulldown_15 (.out(RAMA_HOLD));
  PullDown pulldown_16 (.out(DATA_CK));
  PullDown pulldown_17 (.out(IR_CK));
  PullDown pulldown_18 (.out(PC_CK));
  PullDown pulldown_19 (.out(AC_CK));
  PullDown pulldown_20 (.out(IND_CK));
  PullDown pulldown_21 (.out(LINK_CK));
  PullDown pulldown_22 (.out(RAM_WE));
  PullDown pulldown_23 (.out(RAM_OE));
  PullDown pulldown_24 (.out(MQ_CK));
  and and_189 (i_iac, OPR_IAC, 1'b1);
  and and_190 (i_cll, OPR_CLL, 1'b1);
  and and_191 (i_cma, OPR_CMA, 1'b1);
  and and_192 (i_cml, OPR_CML, 1'b1);
  and and_193 (i_osr, OPR_OSR, 1'b1);
  and and_194 (i_hlt, OPR_HLT, 1'b1);
  or or_33 (i_cla, OPR_CLA1, OPR_CLA2);
  and and_195 (i_nop, OPR_NOP, 1'b1);
  and and_196 (i_ral, OPR_LEFT, ~OPR_X2);  // And
  and and_197 (i_rar, OPR_RIGHT, ~OPR_X2);  // And
  and and_198 (i_rtl, OPR_LEFT, OPR_X2);
  and and_199 (i_rtr, OPR_RIGHT, OPR_X2);
  and and_200 (i_snl, OPR_SNLSZL, ~OPR_TSTINV);  // And
  and and_201 (i_sza, OPR_SZASNA, ~OPR_TSTINV);  // And
  and and_202 (i_sma, OPR_SMASPA, ~OPR_TSTINV);  // And
  and and_203 (i_szl, OPR_SNLSZL, OPR_TSTINV);
  and and_204 (i_sna, OPR_SZASNA, OPR_TSTINV);
  and and_205 (i_spa, OPR_SMASPA, OPR_TSTINV);
  and and_206 (i_skp, ~OPR_SNLSZL, ~OPR_SZASNA, ~OPR_SMASPA, OPR_TSTINV);  // And

  // Other names for the same wires on the sheet: RAMADDR[11:0] = {RA3, RA2, RA1, RA0}; PI0[2:0] = PCIN[2:0];
  //   PI1[2:0] = PCIN[5:3]; PI2[2:0] = PCIN[8:6]; PI3[2:0] = PCIN[11:9]; AC0[2:0] = AC[2:0]; AC1[2:0] = AC[5:3];
  //   AC2[2:0] = AC[8:6]; AC3[2:0] = AC[11:9]; IR0[2:0] = BUS_IR[2:0]; IR1[2:0] = BUS_IR[5:3]; IR2[2:0] = BUS_IR[8:6];
  //   IR3[2:0] = BUS_IR[11:9]; PC0[2:0] = BUS_PC[2:0]; PC1[2:0] = BUS_PC[5:3]; PC2[2:0] = BUS_PC[8:6];
  //   PC3[2:0] = BUS_PC[11:9]; DATA[11:0] = {DA3, DA2, DA1, DA0};
  //   STATUS12 (some bits) = {LINK, IRQ_BUS, IRQ_INHIBIT, FLAG_GIE}; INDOUT[11:0] = {IND3, IND2, IND1, IND0};
  //   MQ0[2:0] = MQ[2:0]; MQ1[2:0] = MQ[5:3]; MQ2[2:0] = MQ[8:6]; MQ3[2:0] = MQ[11:9]; RD0[2:0] = RAMDATA[2:0];
  //   RD1[2:0] = RAMDATA[5:3]; RD2[2:0] = RAMDATA[8:6]; RD3[2:0] = RAMDATA[11:9]; XTAL = clk

  // Notes on the sheet:
  //   clk: Hz: 50000
  //   PC
  //   IR
  //   AC
  //   MQ
  //   IND
  //   RAM-A
  //   RAM-D
  //   PC-IN
  //   DATA
  //   PCIN
  //   SEQ OPR 1 MICROCODES
  //   ------------------------------------
  //   1 CLA CLL
  //   2 CMA CML
  //   3 IAC
  //   4 RAR RAL RTR RTL BSW
  //   ACCUMULATOR
  //   ION
  //   SKON
  //   NOP
  //   AND
  //   TAD
  //   IOF
  //   CLA
  //   CLL
  //   ISZ
  //   STATE
  //   INSTRUCTION
  //   RUN
  //   HALT
  //   PC=0200
  //   BREAKPOINT
  //   C
  //   LINK
  //   PCOUT
  //   SRQ
  //   CMA
  //   DCA
  //   START/STOP/STEP
  //   CLOCK CYCLE CONTROLLER
  //   RTF
  //   GTF
  //   CML
  //   JMS
  //   JMP
  //   SGT
  //   IAC
  //   IOT
  //   MAIN DATA-PATHS
  //   RAMADDR
  //   CAF
  //   RAR
  //   OPR
  //   KCF
  //   RTR
  //   DIR
  //   contents of eeprom_1 (hex, n*v repeats v):
  //   f02,f02,f02,f02,f02,f02,f02,f02,205,f02,f02,f02,f02,f02,f02,f02,f02,f02,f02,f02,f02,
  //   f02,f02,f02,f02,f02,f02,f02,f02,f02,f02,f02,f02,f02,f02,f02,f02,f02,f02,f02,f02,f02,
  //   f02,f02,f02,f02,f02,f02,f02,f02,f02,f02,f02,f02,f02,f02,f02,f02,f02,f02,f02,f02,f02,
  //   f02,f02,f02,f02,f02,f02,f02,f02,f02,f02,f02,f02,f02,f02,f02,f02,f02,f02,f02,f02,f02,
  //   f02,f02,f02,f02,f02,f02,f02,f02,f02,f02,f02,f02,f02,f02,f02,f02,f02,f02,f02,f02,f02,
  //   f02,f02,f02,f02,f02,f02,f02,f02,f02,f02,f02,f02,f02,f02,f02,f02,f02,f02,f02,f02,f02,
  //   f02,f02,c20,e80,308,f28,f02,887,a81,86,c21,a88,c26,b87,a,a,c1,f6,e1,e9,ec,e1,e2,ec,
  //   e5,a0,f3,ef,e6,f4,f7,e1,f2,e5,f3,ba,a,ad,ad,ad,ad,ad,ad,ad,ad,ad,ad,ad,ad,ad,ad,ad,
  //   ad,ad,ad,ad,ad,a,30,30,3a,20,70,72,69,6e,74,68,65,6c,70,2e,62,69,6e,20,20,20,20,20,
  //   20,20,20,20,20,50,43,3a,30,32,30,30,20,2d,20,54,68,69,73,20,68,65,6c,70,d,30,31,3a,
  //   20,44,30,41,42,2d,49,6e,73,74,54,65,73,74,2d,31,2e,70,74,20,20,20,20,20,50,43,3a,
  //   30,32,30,30,2c,20,63,6f,6e,74,20,61,74,20,30,31,34,37,20,2d,20,d,30,32,3a,20,44,30,
  //   42,42,2d,49,6e,73,74,54,65,73,74,2d,32,2e,70,74,20,20,20,20,20,50,43,3a,30,32,30,
  //   30,20,2d,20,d,30,33,3a,20,44,30,49,42,2d,4a,4d,50,4a,4d,53,2e,70,74,20,20,20,20,20,
  //   20,20,20,20,50,43,3a,30,32,30,30,20,2d,20,d,30,34,3a,20,44,30,4a,42,2d,4a,4d,50,4a,
  //   4d,53,2d,52,41,4e,44,4f,4d,2e,70,74,20,20,50,43,3a,30,32,30,30,20,2d,20,d,30,35,3a,
  //   20,44,30,44,42,2d,52,61,6e,64,6f,6d,41,4e,44,2e,70,74,20,20,20,20,20,20,50,43,3a,
  //   30,32,30,30,20,2d,20,d,30,36,3a,20,44,30,43,43,2d,41,64,64,54,65,73,74,2e,70,74,20,
  //   20,20,20,20,20,20,20,50,43,3a,30,32,30,30,20,2d,20,d,30,37,3a,20,46,4f,43,41,4c,2d,
  //   38,2d,4e,4f,49,4e,54,2e,62,6e,20,20,20,20,20,20,20,50,43,3a,30,32,30,30,20,2d,20,
  //   d,bc,e5,ee,e4,be,d,0,f02,f02,f02,f02,f02,f02,f02,f02,f02,f02,f02,f02,f02,f02,f02,
  //   f02,f02,f02,f02,f02,f02,f02,f02,f02,f02,f02,f02,f02,f02,f02,f02,f02,f02,f02,f02,f02,
  //   f02,f02,f02,f02,f02,f02,f02,f02,f02,f02,f02,f02,f02,f02,f02,f02,f02,f02,f02,f02,f02,
  //   f02,f02,f02,f02,f02,f02,f02,f02,f02,f02,f02,f02,f02,f02,f02,f02,f02,f02,f02,f02,f02,
  //   f02,f02,f02,f02,f02,f02,f02,f02,f02,f02,f02,f02,f02,f02,f02,f02,f02,f02,f02,f02,f02,
  //   f02,f02,f02,f02,f02,f02,f02,f02,f02,f02,f02,f02,f02,f02,f02,f02,f02,f02,f02,f02,f02,
  //   f02,f02,f02,f02,f02,f02,f02,f02,f02,f02,f02,f02,f02,f02,f02,f02,f02,f02,f02,f02,f02,
  //   f02,f02,f02,f02,f02,f02,f02,f02,f02,f02,f02,f02,f02,f02,f02,f02,f02,f02,f02,f02,f02,
  //   f02,f02,f02,f02,f02,f02,f02,f02,f02,f02,f02,f02,f02,f02,f02,f02,f02,f02,f02,f02,f02,
  //   f02,f02,f02,f02,f02,f02,f02,f02,f02,f02,f02,f02,f02,f02,f02,f02,f02,f02,f02,f02,f02,
  //   f02,f02,f02,f02,f02,f02,f02,f02,f02,f02,f02,f02,f02,f02,f02,f02,f02,f02,f02,f02,f02,
  //   f02,f02,f02,f02,f02,f02,f02,f02,f02,f02,f02,f02,f02,f02,f02,f02,f02,f02,f02,f02,f02,
  //   f02,f02,f02,f02,f02,f02,f02,f02,f02,f02,f02,f02,f02,f02,f02,f02,f02,f02,f02,f02,f02,
  //   f02,f02,f02,f02,f02,f02,f02,f02,f02,f02,f02,f02,f02,f02,f02,f02,f02,f02,f02,f02,f02,
  //   f02,f02,f02,f02,f02,f02,f02,f02,f02,f02,f02,f02,f02,f02,f02,f02,f02,f02,f02,f02,f02,
  //   f02,f02,f02,f02,f02,f02,f02,f02,f02,f02,f02,f02,f02,f02,f02,f02,f02,f02,f02,f02,f02,
  //   f02,f02,f02,f02,f02,f02,f02,f02,f02,f02,f02,f02,f02,f02,f02,f02,f02,f02,f02,f02,f02,
  //   f02,f02,f02,f02,f02,f02,f02,f02,f02,f02,f02,f02,f02,f02,f02,f02,f02,f02,f02,f02,f02,
  //   f02,f02,f02,f02,f02,f02,f02,f02,f02,f02,f02,f02,f02,f02,f02,f02,f02,f02,f02,f02,f02,
  //   f02,f02,f02,f02,f02,f02,f02,f02,f02,f02,f02,f02,f02,f02,f02,f02,f02,f02,f02,f02,f02,
  //   f02,f02,f02,f02,f02,f02,f02,f02,f02,f02,f02,f02,f02,f02,f02,f02,f02,f02,f02,f02,f02,
  //   f02,f02,f02,f02,f02,f02,f02,f02,f02,f02,f02,f02,f02,f02,f02,f02,f02,f02,f02,f02,f02,
  //   f02,f02,f02,f02,f02,f02,f02,f02,f02,f02,f02,f02,f02,f02,f02,f02,f02,f02,f02,f02,f02,
  //   f02,f02,f02,f02,f02,f02,f02,f02,f02,f02,f02,f02,f02,f02,f02,f02,f02,f02,f02,f02,f02,
  //   f02,f02,f02,f02,f02,f02,f02,f02,f02,f02,f02,f02,f02,f02,f02,f02,f02,f02,f02,f02,f02,
  //   f02,f02,f02,f02,f02,f02,f02,f02,f02,f02,f02,f02,f02,f02,f02,f02,f02,f02,f02,f02,f02,
  //   f02,f02,f02,f02,f02,f02,f02,f02,f02,f02,f02,f02,f02,f02,f02,f02,f02,f02,f02,f02,f02,
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  //   KSF
  //   RAL
  //   RTL
  //   RAMDATA
  //   KCC
  //   SKP
  //   AUTO
  //   IND
  //   KRS
  //   KIE
  //   SMA
  //   CURR
  //   PAGE
  //   KRB
  //   SZA
  //   SNA
  //   SPA
  //   OSR
  //   TFL
  //   TSF
  //   SNL
  //   TCF
  //   SZL
  //   TPC
  //   SWITCHES
  //   ROTATES
  //   TSK
  //   TLS
  //   HLT
  //   INDOUT
  //   PDP-8/X
  //   Rev 0.2
  //   github.com/SmallRoomLabs/PDP8-X
  //   LATCHED
  //   DATA
  //   STEP
  //   PHASE
  //   LATCHED PC
  //   F
  //   S
  //   INC
  //   0=Instructions1 
  //   1=Instructions2
  //   2=JMPJMS-Basic
  //   3=JMPJMS-Random
  //   4=AND-Random 
  //   5=Adder
  //   6=
  //   7=
  //   8=
  //   9=
  //   10=
  //   11=
  //   12=
  //   13=
  //   14=
  //   15=
  //   16=
  //   17=
  //   18=
  //   19=
  //   20=
  //   21=
  //   22=
  //   23=
  //   24=
  //   25=
  //   26=
  //   27=
  //   28=
  //   29=
  //   30=
  //   31=FOCAL8
  //   -
  //   BANK #
  //   L
  //   SEQ OPR 2 MICROCODES
  //   ------------------------------------
  //   1 SMA SPA SZA SZN SNK SZL SKP
  //   2 CLA
  //   3 OSR
  //   4 HLT
  //   SKIP LOGIC
  //   AUTOINDEX
  //   INDIRECT
  //   AC negative
  //   AC=0
  //   LINK<>0
  //   SMA      7500  skip on minus AC
  //   SPA      7510  skip on plus AC
  //   SZA      7440  skip on zero AC
  //   SNA      7450  skip on non-zero AC
  //   SNL      7420  skip on non-zero link
  //   SZL      7430  skip on zero link
  //   AND i
  //   IND
  //   STEP1
  //   IND
  //   STEP2
  //   FETCH OP &
  //   INCREMENT PC
  //   FORCE 4000
  //   INTERRUPT TO IR
  //   AND-i-auto
  //   iAuto 1
  //   iAuto 2
  //   iAuto 3
  //   iAuto 4
  //   603x - KEYBOARD
  //   INSTRUCTIONS
  //   Keyboard Clear Flags
  //   Keyboard and AC Clear
  //   Keyboard Skip if Flag
  //   Keyboard Read Static
  //   Keyboard Read and Begin next read
  //   Keyboard Interrupt Enable
  //   600x - INTERRUPT
  //   INSTRUCTIONS
  //   Turn interrupt ON
  //   Turn interrupt OFF
  //   Clear All Flags
  //   Skip if interrupt ON, and turn OFF
  //   Skip interrupt request
  //   TAD
  //   STEP1
  //   TAD
  //   STEP2
  //   External IRQ
  //   sources
  //   TAD i
  //   Skip on Greater Than flag
  //   Get interrupt flags
  //   Teleprinter Print Character
  //   Teleprinter Load and Start
  //   Teleprinter Flag set (aka SPF)
  //   Teleprinter Clear Flag
  //   Teleprinter Skip if Flag
  //   Teleprinter Skip (aka SPI)
  //   Restore interrupt flags
  //   604x - PRINTER
  //   INSTRUCTIONS
  //   TAD-i-auto
  //   Get address
  //   of M
  //   Save value
  //   from M
  //   indo LATDAT
  //   SKIP IF
  //   AC=ZERO
  //   ISZ i
  //   Save value
  //   from IND
  //   indo LATDAT
  //   ISZ-i-auto
  //   DCA i
  //   DCA-i-auto
  //   Prepare to store
  //   return address
  //   Actually store
  //   return address
  //   Prepare to 
  //   set PC
  //   Actually set
  //   PC
  //   Increment PC
  //   Prepate to store 
  //   return addr
  //   to [ind]
  //   Store return addr
  //   to [ind]
  //   Pause to accept
  //   new PC inc clk
  //   Actually increment
  //   PC
  //   JMS i
  //   JMS i-auto
  //   Prepare to set
  //   new PC
  //   Actually set
  //   new PC
  //   JMP i
  //   Prepare to set PC
  //   with new vector
  //   JMP i-auto
  //   OPR 1
  //   OPR 2
  //   OPR 3
  //   IOT DECODER
  //   604x
  //   TTY PRINTER
  //   SLOW PUNCH
  //   603x
  //   TTY KEYBOARD
  //   SLOW READER
  //   600x
  //   CPU FLAGS & 
  //   INTERRUPT
  //   Keyboard Clear and read Character
  //   OPR_SWP
  //   IR DECODER
  //   OPR DECODER
  //   IOT DECODER
  //   FOR LEDs
endmodule
